# Fritzing sketch PCF8574 (saved by Fritzing 0.9.1b)
breadboards: 1

parts:
  U1 = PCF8574 [package="DIP16 [THT]"]
  Part1 = Arduino Uno (Rev3)
  R1 = Resistor [tolerance=±5% resistance=330 package="0805 [SMD]"]
  R2 = Resistor [tolerance=±5% resistance=330 package="0805 [SMD]"]
  R3 = Resistor [tolerance=±5% resistance=330 package="0805 [SMD]"]
  R4 = Resistor [tolerance=±5% resistance=330 package="0805 [SMD]"]
  R5 = Resistor [tolerance=±5% resistance=330 package="0805 [SMD]"]
  R6 = Resistor [tolerance=±5% resistance=330 package="0805 [SMD]"]
  R7 = Resistor [tolerance=±5% resistance=330 package="0805 [SMD]"]
  R8 = Resistor [tolerance=±5% resistance=330 package="0805 [SMD]"]

nets:
  GND: U1.A0, U1.A1, U1.A3, U1.GND, Part1.GND
  N1: U1.P0, R8.Pin_1
  N2: U1.P1, R7.Pin_1
  N3: U1.P2, R6.Pin_1
  N4: U1.P3, R5.Pin_1
  N5: U1.P4, R4.Pin_0
  N6: U1.P5, R3.Pin_0
  N7: U1.P6, R2.Pin_0
  N8: U1.P7, R1.Pin_0
  N9: U1.SCL, Part1.A5/SCL
  N10: U1.SDA, Part1.A4/SDA
  VCC: U1.VCC, Part1.5V
