# Fritzing sketch accelerometer-MMA8452 (saved by Fritzing 0.9.2b)
breadboards: 2

parts:
  3-Axis_Accelerometer1 = 3-Axis Accelerometer Breakout - MMA8452Q
  Part1 = Logic Level Converter
  Part2 = Arduino Uno (Rev3)
  Part3 = Arduino Uno (Rev3)
  3-Axis_Accelerometer2 = 3-Axis Accelerometer Breakout - MMA8452Q
  R1 = Resistor [tolerance=±5% resistance=220 package="0805 [SMD]"]
  R2 = Resistor [tolerance=±5% resistance=220 package="0805 [SMD]"]

nets:
  3.3V: 3-Axis_Accelerometer1.3.3V, Part1.LV, Part2.3V3
  N1: 3-Axis_Accelerometer1.SDA, Part1.TX_LV
  N2: 3-Axis_Accelerometer1.SCL, Part1.RX_LV
  GND: 3-Axis_Accelerometer1.GND, Part1.GND, Part2.GND
  N3: Part1.TX_HV, Part2.A4/SDA
  N4: Part1.RX_HV, Part2.A5/SCL
  N5: Part1.HV, Part2.5V
  N6: Part3.A4/SDA, R1.Pin_1
  N7: Part3.A5/SCL, R2.Pin_1
  3V3: Part3.3V3, 3-Axis_Accelerometer2.3.3V
  GND_2: Part3.GND, 3-Axis_Accelerometer2.GND
  N8: 3-Axis_Accelerometer2.SDA, R1.Pin_0
  N9: 3-Axis_Accelerometer2.SCL, R2.Pin_0

notes:
  Arduino UNO shown for reference only. Component is supported wherever I2C is supported.
