# Fritzing sketch accelerometer-adxl345 (saved by Fritzing 0.9.0b)

parts:
  Part3 = Arduino Uno (Rev3)
  Part4 = Triple Axis Accelerometer Breakout - ADXL345
  Part5 = Arduino Uno (Rev3)
  Part6 = Triple Axis Accelerometer Breakout - ADXL345

nets:
  N1: Part3.A4/SDA, Part4.SDA
  N2: Part3.A5/SCL, Part4.SCL
  5V: Part3.5V, Part4.VCC, Part4.CS
  GND: Part3.GND, Part4.GND, Part4.SDO
  N3: Part5.A4/SDA, Part6.SDA
  N4: Part5.A5/SCL, Part6.SCL
  5V_2: Part5.5V, Part6.VCC, Part6.CS
  GND_2: Part5.GND, Part6.GND

notes:
  SparkFun
  RioRand
  The AdaFruit version only requires Ground, VCC, SDA and SCL wiring.
