# Fritzing sketch accelerometer-mma7361 (saved by Fritzing 0.9.1b)

parts:
  Part2 = Arduino Uno (Rev3)
  U2 = MMA7361 [package=lga14]

nets:
  N1: Part2.A0, U2.XOUT
  N2: Part2.A1, U2.YOUT
  N3: Part2.A2, U2.ZOUT
  N4: Part2.D13/SCK, U2.SLEEP
  3V3: Part2.3V3, U2.VSS
  N5: Part2.GND, U2.G

notes:
  Alternatively, connect Sleep pin to 5V with 10K resistor in series if you don't want to enable/disable via software.s

custom parts:
  MMA7361: 3-axis 1.5/6g analog output accelerometer
