# Fritzing sketch attiny-programmer (saved by Fritzing 0.8.7b)

parts:
  proto1 = Adafruit_PermaProto_1_4_Board
  U1 = ATTINY45 [package=dip]
  C1 = Electrolytic Capacitor [capacitance=10µF voltage=50V package="0405 [SMD, electrolytic]"]
  LED2 = smd LED [color="Red (633nm)" package="0603 [SMD]"]
  Part1 = Arduino Uno (Rev3)

nets:
  N1: proto1.connectorC9, proto1.connectorC13
  N2: proto1.connectorD6, Part1.D10_PWM/SS
  N3: proto1.connectorD14, Part1.RESET
  N4: proto1.connectorE9, proto1.connectorZ10
  N5: proto1.connectorW2, Part1.5V
  N6: proto1.connectorW3, proto1.connectorY3
  N7: proto1.connectorX1, Part1.GND
  N8: proto1.connectorX2, proto1.connectorZ2
  N9: proto1.connectorY6, U1.VCC
  N10: U1.PB4(ADC2), LED2.anode
  N11: U1.GND, C1.-, LED2.cathode
  N12: U1.PB0(MOSI), Part1.D11_PWM/MOSI
  N13: U1.PB1(MISO), Part1.D12/MISO
  N14: U1.PB2(SCK_ADC1), Part1.D13/SCK
