# Fritzing sketch attiny-slave (saved by Fritzing 0.9.1b)

parts:
  Part2 = Arduino Prototyping Shield
  U1 = ATTINY45 [package=dip]

nets:
  +5V: Part2.+5V, Part2.N$235, U1.VCC
  N1: Part2.SDA, Part2.N$268, U1.PB0(MOSI)
  N2: Part2.SCL, Part2.N$236, U1.PB2(SCK_ADC1)
  GND: Part2.GND, Part2.N$263, U1.GND
  N3: Part2.N$239, U1.PB1(MISO)
  N4: Part2.N$259, U1.PB5(NRES)
  N5: Part2.N$261, U1.PB3(ADC3)
  N6: Part2.N$262, U1.PB4(ADC2)
