# Fritzing sketch ball-switch (saved by Fritzing 0.8.4b)
breadboards: 1

parts:
  Part1 = Arduino Uno (Rev3)
  S1 = Tilt Switch [package=THT]
  R1 = Resistor [tolerance=±5% resistance=10k package=THT]

nets:
  N1: Part1.GND, S1.Pin_2
  N2: Part1.D7, S1.Pin_1, R1.Pin_1
  N3: Part1.5V, R1.Pin_0
