# Fritzing sketch barometer-mpl3115a2 (saved by Fritzing 0.9.1b)
breadboards: 1

parts:
  Part2 = Arduino Uno (Rev3)
  Part3 = Altitude/Pressure Sensor - MPL3115A2 Breakout [part_number=SEN-11084]
  Part4 = Arduino Uno (Rev3)
  R5 = Resistor [tolerance=±1% resistance=330 package="0603 [SMD]"]
  R6 = Resistor [tolerance=±2% resistance=330 package="0603 [SMD]"]
  Part6 = Altitude/Pressure Sensor - MPL3115A2 Breakout [part_number=SEN-11084]

nets:
  N1: Part2.A4/SDA, R5.Pin_0
  N2: Part2.A5/SCL, R6.Pin_0
  3V3: Part2.3V3, Part3.VCC
  GND: Part2.GND, Part3.GND
  N3: Part3.SDA, R5.Pin_1
  N4: Part3.SCL, R6.Pin_1
  N5: Part4.A4/SDA, Part6.SCL
  N6: Part4.A5/SCL, Part6.SDA
  3V3_2: Part4.3V3, Part6.VCC
  GND_2: Part4.GND, Part6.GND

notes:
  For SparkFun MPL3115A2 use 330Ω Resistors

custom parts:
  Altitude/Pressure Sensor - MPL3115A2 Breakout: Life has its ups and downs, so why not measure them? The MPL3115A2 is a MEMS pressure sensor that provides Altitude data to within 30cm (with oversampling enabled). The sensor outputs are digitized by a high resolution 24-bit ADC and transmitted over I2C, meaning it's easy to interface with most controllers. Pressure output can be resolved with output in fractions of a Pascal, and Altitude can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
