# Fritzing sketch board-multi (saved by Fritzing 0.7.12b)

parts:
  Arduino1 = Arduino
  Arduino2 = Arduino
  LED1 = LED - 5mm [color="Red (633nm)" package="5 mm [THT]"]
  LED2 = LED - 5mm [color="Red (633nm)" package="5 mm [THT]"]

nets:
  N1: Arduino1.GND, LED1.cathode
  N2: Arduino1.D13, LED1.anode
  N3: Arduino2.GND, LED2.cathode
  N4: Arduino2.D13, LED2.anode

notes:
  A
  B
