# Fritzing sketch button-bumper (saved by Fritzing 0.7.5b)
breadboards: 1

parts:
  Arduino2 = Arduino
  LED1 = LED - 5mm [color="Red (633nm)" package="5 mm [THT]"]
  R1 = Resistor [tolerance=±5% resistance=10k package=THT]
  S1 = Round Pushbutton

nets:
  N1: Arduino2.GND, LED1.cathode, R1.Pin_1
  N2: Arduino2.D13, LED1.anode
  N3: Arduino2.D7, R1.Pin_0, S1.leg0
  N4: Arduino2.+5V, S1.leg1

notes:
  10k OHM Resister
