# Fritzing sketch button-collection-AT42QT1070 (saved by Fritzing 0.9.1b)

parts:
  BREAKOUT1 = AT42QT1070 5-Channel Capacitive Touch Breakout
  Part2 = Arduino Uno (Rev3)

nets:
  GND: BREAKOUT1.GND, BREAKOUT1.supply_voltage, Part2.GND
  N1: BREAKOUT1.OUTPUT_0, Part2.D6_PWM
  N2: BREAKOUT1.OUTPUT_1, Part2.D5_PWM
  N3: BREAKOUT1.OUTPUT_2, Part2.D4
  N4: BREAKOUT1.OUTPUT_3, Part2.D3_PWM
  N5: BREAKOUT1.OUTPUT_4, Part2.D2

notes:
  Interact with the contacts on this side.
