# Fritzing sketch button-options (saved by Fritzing 0.7.1b)
breadboards: 1

parts:
  Arduino3 = Arduino
  S1 = Pushbutton [package="[THT]"]
  R1 = Resistor [tolerance=±5% resistance=10k package=THT]

nets:
  N1: Arduino3.D8, S1.Pin_1, S1.Pin_2, R1.Pin_0
  N2: Arduino3.+5V, S1.Pin_3, S1.Pin_4
  N3: Arduino3.GND, R1.Pin_1

notes:
  blue: button signal line
  red: +5 power
  black: ground (10kohm resistor)
