# Fritzing sketch compass-MAG3110-tessel (saved by Fritzing 0.9.1b)

parts:
  Part5 = MAG3110
  Part6 = Tessel 2

nets:
  GND: Part5.GND, Part6.GND
  VCC: Part5.VCC, Part6.3V3
  N1: Part5.SDA, Part6.1

custom parts:
  MAG3110: Sparkfun MAG3110 Breakout
  Tessel 2: Draft version of Tessel 2
