# Fritzing sketch compass-hmc6352 (saved by Fritzing 0.9.1b)

parts:
  Part1 = Compass Module - HMC6352
  Part2 = Arduino Uno (Rev3)

nets:
  GND: Part1.GND, Part2.GND
  VCC: Part1.VCC, Part2.5V
  N1: Part1.SDA, Part2.A4/SDA
  N2: Part1.SCL, Part2.A5/SCL
