# Fritzing sketch esc-PCA9685-b (saved by Fritzing 0.9.1b)

parts:
  Part1 = Arduino Uno (Rev3)
  PWM1 = PCA9685 16x12-bit PWM Breakout
  M1 = ESC
  920KV_Motor1 = DJI 920 KV Motor
  Power_plug2 = Power plug  # not connected

nets:
  N1: Part1.A4/SDA, PWM1.no_name_yet#504
  N2: Part1.A5/SCL, PWM1.no_name_yet#503
  N3: Part1.5V, PWM1.no_name_yet#505
  GND: Part1.GND, PWM1.no_name_yet#501, PWM1.no_name_yet#1001, M1.GND
  N4: PWM1.no_name_yet#1, M1.DATA
  N5: M1.U, 920KV_Motor1.u
  N6: M1.V, 920KV_Motor1.v
  N7: M1.W, 920KV_Motor1.w

notes:
  V+ is INTENTIONALLY left disconnected.

custom parts:
  DJI 920 KV Motor: DJI Brushless Outrunner 2212/920K Motor F330-550
