# Fritzing sketch esc-array (saved by Fritzing 0.9.2b)
breadboards: 1

parts:
  Part1 = Arduino Uno (Rev3)
  Power_plug2 = Power plug  # not connected
  M2 = ESC
  920KV_Motor2 = DJI 920 KV Motor
  M3 = ESC
  920KV_Motor3 = DJI 920 KV Motor

nets:
  N1: Part1.D3_PWM, M3.DATA
  N2: Part1.D5_PWM, M2.DATA
  GND: Part1.GND, M2.GND, M3.GND
  N3: M2.U, 920KV_Motor2.u
  N4: M2.V, 920KV_Motor2.v
  N5: M2.W, 920KV_Motor2.w
  N6: M3.U, 920KV_Motor3.u
  N7: M3.V, 920KV_Motor3.v
  N8: M3.W, 920KV_Motor3.w

custom parts:
  DJI 920 KV Motor: DJI Brushless Outrunner 2212/920K Motor F330-550
