# Fritzing sketch esc-bidirectional-forward-reverse (saved by Fritzing 0.9.1b)

parts:
  Part1 = Arduino Uno (Rev3)
  Power_plug2 = Power plug  # not connected
  R1 = Rotary Potentiometer (Small) [maximum_resistance=100kΩ package=THT]
  M2 = ESC
  M3 = DC Motor

nets:
  N1: Part1.A0, R1.leg2
  N2: Part1.D11_PWM/MOSI, M2.DATA
  N3: Part1.5V, R1.leg1
  GND: Part1.GND, R1.wiper, M2.GND
  N4: M2.U, M3.pin_1
  N5: M2.V, M3.pin_2
