# Fritzing sketch esc-dualshock (saved by Fritzing 0.8.7b)

parts:
  Part1 = Arduino Uno (Rev3)
  920KV_Motor1 = DJI 920 KV Motor
  Power_plug1 = Power plug  # not connected
  M1 = ESC

nets:
  N1: Part1.D9_PWM, M1.DATA
  GND: Part1.GND, M1.GND
  N2: 920KV_Motor1.w, M1.W
  N3: 920KV_Motor1.v, M1.V
  N4: 920KV_Motor1.u, M1.U

custom parts:
  DJI 920 KV Motor: DJI Brushless Outrunner 2212/920K Motor F330-550
