# Fritzing sketch escs-2-controllers (saved by Fritzing 0.9.2b)
breadboards: 1

parts:
  Part1 = Arduino Uno (Rev3)
  Power_plug2 = Power plug  # not connected
  M2 = ESC
  920KV_Motor2 = DJI 920 KV Motor
  M3 = ESC
  920KV_Motor3 = DJI 920 KV Motor
  PWM2 = PCA9685 16x12-bit PWM Breakout

nets:
  N1: Part1.A4/SDA, PWM2.no_name_yet#504
  N2: Part1.A5/SCL, PWM2.no_name_yet#503
  N3: Part1.D3_PWM, M3.DATA
  N4: Part1.5V, PWM2.no_name_yet#505
  GND: Part1.GND, M2.GND, M3.GND, PWM2.no_name_yet#501, PWM2.no_name_yet#1000
  N5: M2.U, 920KV_Motor2.u
  N6: M2.V, 920KV_Motor2.v
  N7: M2.W, 920KV_Motor2.w
  N8: M2.DATA, PWM2.no_name_yet#0
  N9: M3.U, 920KV_Motor3.u
  N10: M3.V, 920KV_Motor3.v
  N11: M3.W, 920KV_Motor3.w

custom parts:
  DJI 920 KV Motor: DJI Brushless Outrunner 2212/920K Motor F330-550
