# Fritzing sketch expander-74HC595 (saved by Fritzing 0.9.1b)
breadboards: 1

parts:
  U1 = 74HC595 [package="DIP16 [THT]"]
  LED4 = LED - 5mm [color="Red (633nm)" package="5 mm [THT]"]
  R1 = Resistor [tolerance=±5% resistance=330 package=THT]
  LED5 = LED - 5mm [color="Red (633nm)" package="5 mm [THT]"]
  LED6 = LED - 5mm [color="Red (633nm)" package="5 mm [THT]"]
  LED7 = LED - 5mm [color="Red (633nm)" package="5 mm [THT]"]
  LED8 = LED - 5mm [color="Red (633nm)" package="5 mm [THT]"]
  LED9 = LED - 5mm [color="Red (633nm)" package="5 mm [THT]"]
  LED10 = LED - 5mm [color="Red (633nm)" package="5 mm [THT]"]
  LED11 = LED - 5mm [color="Red (633nm)" package="5 mm [THT]"]
  R2 = Resistor [tolerance=±5% resistance=330 package=THT]
  R3 = Resistor [tolerance=±5% resistance=330 package=THT]
  R4 = Resistor [tolerance=±5% resistance=330 package=THT]
  R5 = Resistor [tolerance=±5% resistance=220 package=THT]
  R6 = Resistor [tolerance=±5% resistance=220 package=THT]
  R7 = Resistor [tolerance=±5% resistance=220 package=THT]
  R8 = Resistor [tolerance=±5% resistance=220 package=THT]
  Arduino1 = Arduino Uno (Rev3)

nets:
  N1: U1.Q1, LED6.anode
  N2: U1.Q2, LED5.anode
  N3: U1.Q3, LED4.anode
  N4: U1.Q4, LED8.anode
  N5: U1.Q5, LED9.anode
  N6: U1.Q6, LED10.anode
  N7: U1.Q7, LED11.anode
  GND: U1.GND, U1.OE, R1.Pin_1, R2.Pin_1, R3.Pin_1, R4.Pin_1, Arduino1.GND
  VCC: U1.MR, U1.VCC, Arduino1.5V
  N8: U1.SH_CP, Arduino1.D3_PWM
  N9: U1.ST_CP, Arduino1.D4
  N10: U1.DS, Arduino1.D2
  N11: U1.Q0, LED7.anode
  N12: LED4.cathode, R1.Pin_0
  N13: LED5.cathode, R2.Pin_0
  N14: LED6.cathode, R3.Pin_0
  N15: LED7.cathode, R4.Pin_0
  N16: LED8.cathode, R5.Pin_1
  N17: LED9.cathode, R6.Pin_1
  N18: LED10.cathode, R7.Pin_1
  N19: LED11.cathode, R8.Pin_1
  N20: R5.Pin_0, R6.Pin_0, R7.Pin_0, R8.Pin_0
