# Fritzing sketch expander-ADS1115-4-pots (saved by Fritzing 0.9.3b)
breadboards: 1

parts:
  Componente1 = Adafruit ADS1115 16Bit I2C ADC [part_number="Adafruit #1085"]
  Componente2 = Arduino Uno (Rev3)
  R1 = Trimmer Potentiometer [maximum_resistance=10kΩ package=THT]
  R2 = Trimmer Potentiometer [maximum_resistance=10kΩ package=THT]
  R3 = Trimmer Potentiometer [maximum_resistance=10kΩ package=THT]
  R4 = Trimmer Potentiometer [maximum_resistance=10kΩ package=THT]

nets:
  N1: Componente1.AIN3, R4.wiper
  N2: Componente1.AIN2, R3.wiper
  N3: Componente1.AIN1, R2.wiper
  N4: Componente1.AIN0, R1.wiper
  N5: Componente1.SDA, Componente2.A4/SDA
  N6: Componente1.SCL, Componente2.A5/SCL
  GND: Componente1.GND, Componente2.GND, R1.leg1, R2.leg1, R4.leg1
  VDD: Componente1.VDD, Componente2.5V, R1.leg2, R2.leg2, R3.leg1, R3.leg2, R4.leg2

custom parts:
  Adafruit ADS1115 16Bit I2C ADC: For microcontrollers without an analog-to-digital converter or when you want a higher-precision ADC, the ADS1115 provides 16-bit precision at 860 samples/second over I2C. The chip can be configured as 4 single-ended input channels, or two differential channels. As a nice bonus, it even includes a programmable gain amplifier, up to x16, to help boost up smaller single/differential signals to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
