# Fritzing sketch expander-CD74HC4067 (saved by Fritzing 0.9.1b)
breadboards: 2

parts:
  Part4 = Arduino Nano (Rev3.0) (ICSP)
  U1 = CD74HC4067 [package=ssop24]
  Part5 = Arduino Uno (Rev3)
  POT1 = Breadboard Trimpot
  POT2 = Breadboard Trimpot
  POT3 = Breadboard Trimpot

nets:
  GND: Part4.GND, U1.GND, Part5.GND, POT1.PIN1, POT2.PIN1, POT3.PIN1
  N1: Part4.D2, U1.S0
  N2: Part4.D3, U1.S1
  N3: Part4.D4, U1.S2
  N4: Part4.D5, U1.S3
  VIN: Part4.VIN, Part5.5V, POT1.PIN3, POT2.PIN3, POT3.PIN3
  5V: Part4.5V, U1.VCC
  N5: Part4.A7, U1.COM
  N6: Part4.A5, Part5.A5/SCL
  N7: Part4.A4, Part5.A4/SDA
  N8: U1.CHAN7, POT3.PIN2
  N9: U1.CHAN0, POT1.PIN2
  N10: U1.CHAN15, POT2.PIN2

notes:
  S0 -> 2 Blue
  S1 -> 3 Purple
  S2 -> 4 Pink
  S3 -> 5 Cyan
  Address Control:
  | 9 | 8 | Addr |
  ---------------------
  | 0 | 0 | 0x0A |
  | 0 | 1 | 0x0B |
  | 1 | 0 | 0x0C |
  | 1 | 1 | 0x0D |

custom parts:
  CD74HC4067: 16-channel analog MUX
