# Fritzing sketch expander-LIS3DH (saved by Fritzing 0.9.2b)

parts:
  Part1 = Adafruit LIS3DH [part_number="Adafruit #2809"]
  Part2 = Arduino Uno (Rev3)
  POT1 = Breadboard Trimpot

nets:
  N1: Part1.ADC2, POT1.PIN2
  VIN: Part1.VIN, Part2.5V
  N2: Part1.3.3V, POT1.PIN1
  GND: Part1.GND, Part2.GND, POT1.PIN3
  N3: Part1.SCL, Part2.A5/SCL
  N4: Part1.SDA, Part2.A4/SDA

custom parts:
  Adafruit LIS3DH: The LIS3DH is a very popular low power triple-axis accelerometer. It's low-cost, but has just about every 'extra' you'd want in an accelerometer: Three axis sensing, 10-bit precision ±2g/±4g/±8g/±16g selectable scaling Both I2C (2 possible addresses) and SPI interface options Interrupt output Multiple data rate options 1 Hz to 5Khz As low as 2uA current draw (just the chip itself, not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
