# Fritzing sketch expander-MCP23017 (saved by Fritzing 0.9.2b)
breadboards: 2

parts:
  Part1 = Arduino Uno (Rev3)
  LED1 = LED - 5mm [color="Blue (430nm)" package="5 mm [THT]"]
  LED2 = LED - 5mm [color="Blue (430nm)" package="5 mm [THT]"]
  LED3 = LED - 5mm [color="Blue (430nm)" package="5 mm [THT]"]
  LED4 = LED - 5mm [color="Blue (430nm)" package="5 mm [THT]"]
  LED5 = LED - 5mm [color="Green (555nm)" package="5 mm [THT]"]
  LED6 = LED - 5mm [color="Green (555nm)" package="5 mm [THT]"]
  LED7 = LED - 5mm [color="Green (555nm)" package="5 mm [THT]"]
  LED8 = LED - 5mm [color="Green (555nm)" package="5 mm [THT]"]
  IC1 = MCP23017 I2C I/O Expander

nets:
  N1: Part1.A4/SDA, IC1.SDA
  N2: Part1.A5/SCL, IC1.SCL
  5V: Part1.5V, IC1.VDD, IC1.RESET
  N3: Part1.GND, LED1.cathode, LED2.cathode, LED3.cathode, LED4.cathode, LED5.cathode, LED6.cathode, LED7.cathode, LED8.cathode, IC1.GPB7, IC1.A0, IC1.A1, IC1.A2
  N4: LED1.anode, IC1.GPB6
  N5: LED2.anode, IC1.GPB0
  N6: LED3.anode, IC1.GPB2
  N7: LED4.anode, IC1.GPB4
  N8: LED5.anode, IC1.GPA6
  N9: LED6.anode, IC1.GPA4
  N10: LED7.anode, IC1.GPA2
  N11: LED8.anode, IC1.GPA0

custom parts:
  MCP23017 I2C I/O Expander: The MCP23017 uses two i2c pins (these can be shared with other i2c devices), and in exchange gives you 16 general purpose pins. You can set each of 16 pins to be input, output, input with a pullup or open drain. There's even the ability to get an interrupt via an external pin when any of the inputs change so you don't have to keep polling the chip.
