# Fritzing sketch expander-MUXSHIELD2-analog-read (saved by Fritzing 0.9.1b)
breadboards: 1

parts:
  R1 = Rotary Potentiometer (Small) [maximum_resistance=100kΩ package=THT]
  R2 = Rotary Potentiometer (Small) [maximum_resistance=100kΩ package=THT]
  Part_1 = MUXSHIELD2

nets:
  N1: R1.leg1, R2.leg1, Part_1.5V
  N2: R1.wiper, Part_1.IO2-15
  N3: R1.leg2, R2.leg2, Part_1.D5, Part_1.GND
  N4: R2.wiper, Part_1.IO1-15

custom parts:
  MUXSHIELD2: 48 Digital IO or Analog Input
