# Fritzing sketch expander-MUXSHIELD2-mixed (saved by Fritzing 0.9.1b)

parts:
  Part_1 = MUXSHIELD2
  DigitalPushButtonV2 = Button Breakout

nets:
  N1: Part_1.D6, Part_1.IO1-1, Part_1.IO3-1
  N2: Part_1.D9, Part_1.IO1-2, Part_1.IO1-3, Part_1.IO3-2, Part_1.IO3-3, DigitalPushButtonV2.Signal
  GND: Part_1.GND, DigitalPushButtonV2.GND
  N3: Part_1.5V, DigitalPushButtonV2.Input
  N4: Part_1.IO1-0, Part_1.IO3-0
  N5: Part_1.IO1-4, Part_1.IO3-4
  N6: Part_1.IO1-5, Part_1.IO3-5
  N7: Part_1.IO1-6, Part_1.IO3-6
  N8: Part_1.IO1-7, Part_1.IO3-7
  N9: Part_1.IO1-8, Part_1.IO3-8
  N10: Part_1.IO1-9, Part_1.IO3-9
  N11: Part_1.IO1-10, Part_1.IO3-10
  N12: Part_1.IO1-11, Part_1.IO3-11
  N13: Part_1.IO1-12, Part_1.IO3-12
  N14: Part_1.IO1-13, Part_1.IO3-13
  N15: Part_1.IO1-14, Part_1.IO3-14
  N16: Part_1.IO1-15, Part_1.IO3-15

custom parts:
  MUXSHIELD2: 48 Digital IO or Analog Input
