# Fritzing sketch expander-PCA9685 (saved by Fritzing 0.9.1b)
breadboards: 1

parts:
  Part1 = Arduino Uno (Rev3)
  PWM1 = PCA9685 16x12-bit PWM Breakout
  LED1 = LED - 5mm [color="Blue (430nm)" package="5 mm [THT]"]
  LED2 = LED - 5mm [color="Blue (430nm)" package="5 mm [THT]"]
  LED3 = LED - 5mm [color="Blue (430nm)" package="5 mm [THT]"]
  LED4 = LED - 5mm [color="Blue (430nm)" package="5 mm [THT]"]
  LED5 = LED - 5mm [color="Green (555nm)" package="5 mm [THT]"]
  LED6 = LED - 5mm [color="Green (555nm)" package="5 mm [THT]"]
  LED7 = LED - 5mm [color="Green (555nm)" package="5 mm [THT]"]
  LED8 = LED - 5mm [color="Green (555nm)" package="5 mm [THT]"]

nets:
  N1: Part1.A4/SDA, PWM1.no_name_yet#504
  N2: Part1.A5/SCL, PWM1.no_name_yet#503
  N3: Part1.5V, PWM1.no_name_yet#505
  N4: Part1.GND, PWM1.no_name_yet#501, PWM1.no_name_yet#1000, LED1.cathode, LED2.cathode, LED3.cathode, LED4.cathode, LED5.cathode, LED6.cathode, LED7.cathode, LED8.cathode
  N5: PWM1.no_name_yet#0, LED8.anode
  N6: PWM1.no_name_yet#2, LED7.anode
  N7: PWM1.no_name_yet#4, LED6.anode
  N8: PWM1.no_name_yet#6, LED5.anode
  N9: PWM1.no_name_yet#8, LED2.anode
  N10: PWM1.no_name_yet#10, LED3.anode
  N11: PWM1.no_name_yet#12, LED4.anode
  N12: PWM1.no_name_yet#14, LED1.anode
