# Fritzing sketch expander-PCF8574-basic (saved by Fritzing 0.9.1b)
breadboards: 1

parts:
  Part1 = Arduino Uno (Rev3)
  LED8 = LED - 5mm [color="Green (555nm)" package="5 mm [THT]"]
  U1 = PCF8574 [package="DIP16 [THT]"]

nets:
  N1: Part1.A4/SDA, U1.SDA
  N2: Part1.A5/SCL, U1.SCL
  5V: Part1.5V, U1.VCC
  GND: Part1.GND, LED8.cathode, U1.GND
  N3: LED8.anode, U1.P4
