# Fritzing sketch expander-PCF8575-basic (saved by Fritzing 0.9.1b)
breadboards: 1

parts:
  Part1 = Arduino Uno (Rev3)
  LED2 = LED - 5mm [color="Blue (430nm)" package="5 mm [THT]"]
  IC2 = PCF8575

nets:
  N1: Part1.A4/SDA, IC2.SDA
  N2: Part1.A5/SCL, IC2.SCL
  5V: Part1.5V, IC2.VCC
  GND: Part1.GND, LED2.cathode, IC2.GND
  N3: LED2.anode, IC2.GPA0
