# Fritzing sketch expander-PCF8575-led-button (saved by Fritzing 0.9.1b)
breadboards: 1

parts:
  Part1 = Arduino Uno (Rev3)
  LED2 = LED - 5mm [color="Blue (430nm)" package="5 mm [THT]"]
  IC2 = PCF8575
  S5 = Pushbutton [package="[THT]"]
  R2 = Resistor [tolerance=±5% resistance=10k package=THT]

nets:
  N1: Part1.A4/SDA, IC2.SDA
  N2: Part1.A5/SCL, IC2.SCL
  5V: Part1.5V, IC2.VCC, S5.Pin_1, S5.Pin_2
  GND: Part1.GND, LED2.cathode, IC2.GND, R2.Pin_0
  N3: LED2.anode, IC2.GPA0
  N4: IC2.GPB7, S5.Pin_3, S5.Pin_4, R2.Pin_1
