# Fritzing sketch expander-PCF8591 (saved by Fritzing 0.9.1b)
breadboards: 1

parts:
  Part1 = Arduino Uno (Rev3)
  IC1 = Microchip PCF8591 4 Channel AD/DA expander [part_number=PCF8591 package="DIP (Dual Inline) [THT]"]
  POT1 = Breadboard Trimpot

nets:
  N1: Part1.A4/SDA, IC1.SCL
  N2: Part1.A5/SCL, IC1.SDA
  5V: Part1.5V, IC1.VREF, IC1.VDD, POT1.PIN1
  GND: Part1.GND, IC1.A0, IC1.A1, IC1.A2, IC1.VSS, IC1.EXT, IC1.AGND, POT1.PIN3
  N3: IC1.AIN0, POT1.PIN2
