# Fritzing sketch flex (saved by Fritzing 0.9.3b)
breadboards: 1

parts:
  Part1 = Arduino Uno (Rev3) - ICSP
  R1 = Basic Flex Resistor
  R2 = Resistor [tolerance=±5% resistance=220 package="0805 [SMD]"]

nets:
  N1: Part1.A2, R1.pin_1, R2.Pin_0
  N2: Part1.5V, R1.Pin_2
  N3: Part1.GND, R2.Pin_1
