# Fritzing sketch gps-GP-20U7 (saved by Fritzing 0.9.3b)

parts:
  Part1 = Arduino Uno (Rev3)
  Part2 = GP-20U7

nets:
  N1: Part1.D11_PWM/MOSI, Part2.TX
  3V3: Part1.3V3, Part2.VCC
  GND: Part1.GND, Part2.GND
