# Fritzing sketch gps-adafruit (saved by Fritzing 0.9.2b)

parts:
  Part1 = Arduino Uno (Rev3)
  GPS1 = Adafruit Ultimate GPS Breakout

nets:
  N1: Part1.D10_PWM/SS, GPS1.RX
  N2: Part1.D11_PWM/MOSI, GPS1.TX
  5V: Part1.5V, GPS1.VIN
  GND: Part1.GND, GPS1.GND
