# Fritzing sketch gps-hardware-serial (saved by Fritzing 0.9.2b)

parts:
  GPS1 = Adafruit Ultimate GPS Breakout
  Part2 = Arduino Mega 2560 (Rev3)

nets:
  N1: GPS1.TX, Part2.D19/RX1
  N2: GPS1.RX, Part2.D18/TX1
  GND: GPS1.GND, Part2.GND
  VIN: GPS1.VIN, Part2.5V
