# Fritzing sketch gps-sparkfun (saved by Fritzing 0.9.2b)

parts:
  Part1 = SparkFun Venus GPS with SMA Connector GPS-11058
  Part2 = Arduino Uno (Rev3)

nets:
  GND: Part1.GND, Part2.GND
  3.3V: Part1.3.3V, Part2.3V3
  N1: Part1.TX0, Part2.D11_PWM/MOSI
  N2: Part1.RX0, Part2.D10_PWM/SS

custom parts:
  SparkFun Venus GPS with SMA Connector GPS-11058: This is the latest version of our Venus GPS board; the smallest, most powerful, and most versatile GPS receiver we carry. It’s based on the Venus638FLPx, the successor to the Venus634LPx. The Venus638FLPx outputs standard NMEA-0183 or SkyTraq Binary sentences at a default rate of 9600bps (adjustable to 115200bps), with update rates up to 20Hz! The Venus638FLPx also allows for limited on-chip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
