# Fritzing sketch gyro-lpr5150l (saved by Fritzing 0.9.1b)

parts:
  Part1 = Arduino Uno (Rev3)
  LPR5150AL1 = LPR5150AL

nets:
  N1: Part1.A0, LPR5150AL1.Xout
  N2: Part1.A1, LPR5150AL1.Yout
  5V: Part1.5V, LPR5150AL1.Vin
  GND: Part1.GND, LPR5150AL1.GND

custom parts:
  LPR5150AL: LPR5150AL gyro Breakout board
