# Fritzing sketch imp-led (saved by Fritzing 0.8.7b)

parts:
  Part1 = Electric Imp April
  LED1 = LED - 5mm [color="Red (633nm)" package="5 mm [THT]"]

nets:
  N1: Part1.6, LED1.anode
  N2: Part1.9, LED1.cathode

custom parts:
  Electric Imp April: Electric Imp Breakout Board with onboard 3.3V regulated power supply
