# Fritzing sketch imu-bno055 (saved by Fritzing 0.9.2b)

parts:
  Part1 = Arduino Uno (Rev3)
  Part2 = 9-DOF Absolute Orientation IMU Fusion Breakout - BNO055

nets:
  N1: Part1.A4/SDA, Part2.SDA_5V
  N2: Part1.A5/SCL, Part2.SCL_5V
  N3: Part1.5V, Part2.5.0V
  GND: Part1.GND, Part2.GND

custom parts:
  9-DOF Absolute Orientation IMU Fusion Breakout - BNO055: A MEMS accelerometer, magnetometer and gyroscope on a single die with a high speed ARM Cortex-M0 based processor to digest all the sensor data, abstract the sensor fusion and real time requirements away, and spit out data you can use in quaternions, Euler angles or vectors.
