# Fritzing sketch imu-lsm303c (saved by Fritzing 0.9.3b)

parts:
  Part1 = Arduino Uno (Rev3)
  Part2 = LSM303C (6 DOF)

nets:
  N1: Part1.A4/SDA, Part2.SDA/SDI/SDO
  N2: Part1.A5/SCL, Part2.SCL/SCLK
  5V: Part1.5V, Part2.VCC
  GND: Part1.GND, Part2.GND
