# Fritzing sketch joystick-motor-led (saved by Fritzing 0.7.1b)
breadboards: 1

parts:
  Arduino1 = Arduino
  M1 = DC Motor
  Part1 = Thumb Joystick
  LED1 = LED - 5mm [color="Red (633nm)" package="5 mm [THT]"]

nets:
  GND: Arduino1.GND, M1.pin_1, Part1.GND, LED1.cathode
  N1: Arduino1.D13, LED1.anode
  N2: Arduino1.D5, M1.pin_2
  +5V: Arduino1.+5V, Part1.VCC
  N3: Arduino1.A0, Part1.VERT
  N4: Arduino1.A1, Part1.HORZ
