# Fritzing sketch joystick-sparkfun (saved by Fritzing 0.8.7b)

parts:
  Part2 = Arduino Uno (Rev3)
  Part3 = Thumb Joystick

nets:
  N1: Part2.A0, Part3.VERT
  N2: Part2.A1, Part3.HORZ
  5V: Part2.5V, Part3.VCC
  GND: Part2.GND, Part3.GND
