# Fritzing sketch joystick (saved by Fritzing 0.9.1b)

parts:
  Part1 = Arduino Uno (Rev3)
  POT1 = Analog Thumb Joystick
  Part2 = Arduino Uno (Rev3)
  Part3 = Thumb Joystick

nets:
  N1: Part1.A0, POT1.Xout
  N2: Part1.A1, POT1.Yout
  5V: Part1.5V, POT1.Vcc
  GND: Part1.GND, POT1.GND
  N3: Part2.A0, Part3.VERT
  N4: Part2.A1, Part3.HORZ
  5V_2: Part2.5V, Part3.VCC
  GND_2: Part2.GND, Part3.GND
