# Fritzing sketch keypad-3X4_I2C_NANO_BACKPACK (saved by Fritzing 0.9.1b)

parts:
  Part5 = Arduino Nano (Rev3.0) (ICSP)
  kEYPAD_MATRICIAL_2 = KEYPAD 4x3

nets:
  N1: Part5.D2, kEYPAD_MATRICIAL_2.arrow4
  N2: Part5.D3, kEYPAD_MATRICIAL_2.arrow3
  N3: Part5.D4, kEYPAD_MATRICIAL_2.col3
  N4: Part5.D5, kEYPAD_MATRICIAL_2.arrow2
  N5: Part5.D6, kEYPAD_MATRICIAL_2.col2
  N6: Part5.D7, kEYPAD_MATRICIAL_2.arrow1
  N7: Part5.D8, kEYPAD_MATRICIAL_2.col1

notes:
  SDA SCL GND 5V
