# Fritzing sketch keypad-MPR121 (saved by Fritzing 0.9.1b)

parts:
  Part1 = MPR121 Breakout
  Part2 = Arduino Uno (Rev3)

nets:
  N1: Part1.SCL, Part2.A5/SCL
  N2: Part1.SDA, Part2.A4/SDA
  3.3V: Part1.3.3V, Part2.3V3
  GND: Part1.GND, Part2.GND
