# Fritzing sketch keypad_4X4_I2C_NANO_BACKPACK (saved by Fritzing 0.9.3b)

parts:
  Part1 = Arduino Nano (Rev3.0)
  Part2 = Arduino Uno (Rev3)
  Matrix_keypad1 = KEYPAD 4x4

nets:
  N1: Part1.D2, Matrix_keypad1.col2
  N2: Part1.D3, Matrix_keypad1.col3
  N3: Part1.D4, Matrix_keypad1.row3
  N4: Part1.D5, Matrix_keypad1.col4
  N5: Part1.D6, Matrix_keypad1.row1
  N6: Part1.D7, Matrix_keypad1.col1
  N7: Part1.D8, Matrix_keypad1.row2
  N8: Part1.D9, Matrix_keypad1.row4
  VIN: Part1.VIN, Part2.5V
  GND: Part1.GND, Part2.GND
  N9: Part1.A5, Part2.A5/SCL
  N10: Part1.A4, Part2.A4/SDA

notes:
  Keypad Row Pins: 7, 2, 3, 5
  Keypad Column Pins: 6, 8, 4, 9
  Make sure all connections to the Nano/I2C board match up.

custom parts:
  KEYPAD 4x4: Matrix keypad 16 buttons, 4 rows x 4 columns
