# Fritzing sketch kinect-arm-controller (saved by Fritzing 0.9.1b)
stripboards: 1

parts:
  Part1 = Arduino Uno (Rev3)
  Part2 = Servo Improved
  Part3 = Servo Improved
  Part4 = Servo Improved
  A1 = Power Source [package=power_jack_combo]

nets:
  N1: Part1.D9_PWM, Part3.signal
  N2: Part1.D10_PWM/SS, Part2.signal
  N3: Part1.D6_PWM, Part4.signal
  GND: Part1.GND, Part2.ground, Part3.ground, Part4.ground, A1.GND1
  VCC: Part2.vcc, Part3.vcc, Part4.vcc, A1.PWR1

notes:
  External Power Source
