# Fritzing sketch lcd-16x2-tessel (saved by Fritzing 0.9.1b)
breadboards: 1

parts:
  U1 = LCD-16X2 [package=lcd-16x2]
  Part1 = Tessel 2
  POT1 = Breadboard Trimpot
  R1 = Resistor [tolerance=±5% resistance=330 package=THT]

nets:
  VSS: U1.VSS, U1.K, Part1.GND, POT1.PIN3
  VDD: U1.VDD, Part1.5V, POT1.PIN1, R1.Pin_1
  N1: U1.VO, POT1.PIN2
  N2: U1.RS, Part1.2
  N3: U1.E, Part1.3
  N4: U1.DB4, Part1.4
  N5: U1.DB5, Part1.5
  N6: U1.DB6, Part1.6
  N7: U1.DB7, Part1.7
  N8: U1.A, R1.Pin_0

notes:
  Contrast control is connected directly to the LCD
  This LCD is a 3.3V device, but must be connected to the 5V source, with a 330Ω resistor. If 5V source is not used, the second row of the display may not operate correctly.

custom parts:
  Tessel 2: Draft version of Tessel 2
