# Fritzing sketch lcd-JHD1313M1 (saved by Fritzing 0.9.2b)

parts:
  Part1 = Arduino Uno (Rev3)  # not connected
  Grove1 = Grove OLED 128x96
  Part2 = Base Shield V2
  Part3 = Arduino Uno (Rev3)
  Grove2 = Grove OLED 128x96

nets:
  N1: Grove1.GND, Part2.pin_124
  N2: Grove1.VCC, Part2.pin_125
  N3: Grove1.SDA, Part2.pin_126
  N4: Grove1.SCL, Part2.pin_127
  N5: Part3.A4/SDA, Grove2.SDA
  N6: Part3.A5/SCL, Grove2.SCL
  5V: Part3.5V, Grove2.VCC
  GND: Part3.GND, Grove2.GND
