# Fritzing sketch lcd-enumeratechars (saved by Fritzing 0.9.1b)
breadboards: 1

parts:
  POT1 = Breadboard Trimpot
  Part1 = Arduino Uno (Rev3)
  U2 = LCD-16X2 [package=lcd-16x2]

nets:
  5V: POT1.PIN1, Part1.5V, U2.VDD, U2.A
  N1: POT1.PIN2, U2.VO
  GND: POT1.PIN3, Part1.GND, U2.VSS, U2.K
  N2: Part1.D8, U2.E
  N3: Part1.D9_PWM, U2.DB4
  N4: Part1.D10_PWM/SS, U2.DB5
  N5: Part1.D11_PWM/MOSI, U2.DB6
  N6: Part1.D12/MISO, U2.DB7
  N7: Part1.D7, U2.RS

notes:
  Contrast control is connected directly to the LCD
