# Fritzing sketch lcd-i2c (saved by Fritzing 0.9.1b)

parts:
  Part1 = Arduino Uno (Rev3)  # not connected
  Grove1 = Grove OLED 128x96
  Part2 = Base Shield V2

nets:
  N1: Grove1.GND, Part2.pin_124
  N2: Grove1.VCC, Part2.pin_125
  N3: Grove1.SDA, Part2.pin_126
  N4: Grove1.SCL, Part2.pin_127
