# Fritzing sketch lcd-pcf8574 (saved by Fritzing 0.9.1b)

parts:
  U1 = LCD-16X2 [package=lcd-16x2]
  Part1 = Arduino Uno (Rev3)

nets:
  VSS: U1.VSS, Part1.GND
  VDD: U1.VDD, Part1.5V
  N1: U1.VO, Part1.A4/SDA
  N2: U1.RS, Part1.A5/SCL

notes:
  The controller name is printed on the chip mounted on the read of the LCD backpack
