# Fritzing sketch lcd-rgb-tessel-grove-JHD1313M1-external (saved by Fritzing 0.9.2b)

parts:
  Part1 = Tessel 2
  Grove1 = Grove RGB LCD

nets:
  N1: Part1.0, Grove1.SCL
  N2: Part1.1, Grove1.SDA
  GND: Part1.GND, Grove1.GND
  5V: Part1.5V, Grove1.VCC

notes:
  The SCL and SDA wires are intentionally crossed due to the conflicting pin order of the two devices.
  Also, the 5V source is intentionally used because this display expects a 4.5-5.5V operating voltage source. The RGB backlight expects 2.3-5.5V.

custom parts:
  Tessel 2: Draft version of Tessel 2
