# Fritzing sketch lcd-runner-20x4 (saved by Fritzing 0.9.1b)
breadboards: 1

parts:
  POT1 = Breadboard Trimpot
  Part1 = Arduino Uno (Rev3)
  LCD1 = LCD screen

nets:
  5V: POT1.PIN1, Part1.5V, LCD1.VDD, LCD1.LED-
  N1: POT1.PIN2, LCD1.V0
  GND: POT1.PIN3, Part1.GND, LCD1.VSS, LCD1.LED+
  N2: Part1.D8, LCD1.E
  N3: Part1.D9_PWM, LCD1.DB4
  N4: Part1.D10_PWM/SS, LCD1.DB5
  N5: Part1.D11_PWM/MOSI, LCD1.DB6
  N6: Part1.D12/MISO, LCD1.DB7
  N7: Part1.D7, LCD1.RS

notes:
  Contrast control is connected directly to the LCD
  Unfortunately, there is no 20x4 LCD Fritzing part available.

custom parts:
  LCD screen: A standard character display, usually with 2x16 characters. Comes in many colors.
