# Fritzing sketch lcd (saved by Fritzing 0.8.7b)
breadboards: 1

parts:
  LCD1 = LCD screen
  R1 = Rotary Potentiometer (Small) [maximum_resistance=100kΩ package=THT]
  Arduino1 = Arduino Uno (Rev3)

nets:
  VSS: LCD1.VSS, LCD1.R/W, LCD1.LED-, R1.leg2, Arduino1.GND
  N1: LCD1.VDD, LCD1.LED+, R1.leg1
  N2: LCD1.V0, R1.wiper
  N3: LCD1.RS, Arduino1.D7
  N4: LCD1.E, Arduino1.D8
