# Fritzing sketch led-13-galileo (saved by Fritzing 0.9.1b)

parts:
  LED1 = LED - 5mm [color="Red (633nm)" package="5 mm [THT]"]
  Part2 = Intel Galileo Gen2

nets:
  N1: LED1.cathode, Part2.GND
  N2: LED1.anode, Part2.D13/SCK
