# Fritzing sketch led-13-mega (saved by Fritzing 0.9.1b)

parts:
  LED1 = LED - 5mm [color="Red (633nm)" package="5 mm [THT]"]
  Part3 = Arduino Mega ADK (Rev3)

nets:
  N1: LED1.cathode, Part3.GND
  N2: LED1.anode, Part3.D13_PWM
