# Fritzing sketch led-PCA9685 (saved by Fritzing 0.9.1b)
breadboards: 1

parts:
  Part1 = Arduino Uno (Rev3)
  PWM1 = PCA9685 16x12-bit PWM Breakout
  LED1 = LED - 3mm [color="Green (555nm)" package="3 mm [THT]"]

nets:
  N1: Part1.A4/SDA, PWM1.no_name_yet#504
  N2: Part1.A5/SCL, PWM1.no_name_yet#503
  N3: Part1.5V, PWM1.no_name_yet#505
  N4: Part1.GND, PWM1.no_name_yet#501
  N5: PWM1.no_name_yet#0, LED1.anode
  N6: PWM1.no_name_yet#100, LED1.cathode
