# Fritzing sketch led-array-2-controllers (saved by Fritzing 0.9.2b)
breadboards: 1

parts:
  Part1 = Arduino Uno (Rev3)
  LED1 = smd LED [color="Red (633nm)" package="1206 [SMD]"]
  LED2 = smd LED [color="Green (555nm)" package="1206 [SMD]"]
  LED3 = smd LED [color="Blue (430nm)" package="1206 [SMD]"]
  PWM2 = PCA9685 16x12-bit PWM Breakout

nets:
  N1: Part1.A4/SDA, PWM2.no_name_yet#604
  N2: Part1.A5/SCL, PWM2.no_name_yet#603
  N3: Part1.D3_PWM, LED1.anode
  N4: Part1.5V, PWM2.no_name_yet#606
  N5: Part1.GND, LED1.cathode, LED2.cathode, LED3.cathode, PWM2.no_name_yet#601, PWM2.no_name_yet#1000, PWM2.no_name_yet#1002
  N6: LED2.anode, PWM2.no_name_yet#1
  N7: LED3.anode, PWM2.no_name_yet#0
