# Fritzing sketch led-array (saved by Fritzing 0.9.0b)
breadboards: 1

parts:
  Part1 = Arduino Uno (Rev3)
  LED1 = smd LED [color="Red (633nm)" package="1206 [SMD]"]
  LED2 = smd LED [color="Green (555nm)" package="1206 [SMD]"]
  LED3 = smd LED [color="Blue (430nm)" package="1206 [SMD]"]

nets:
  N1: Part1.D3_PWM, LED1.anode
  N2: Part1.D5_PWM, LED2.anode
  N3: Part1.D6_PWM, LED3.anode
  N4: Part1.GND, LED1.cathode, LED2.cathode, LED3.cathode
