# Fritzing sketch led-demo-sequence (saved by Fritzing 0.8.7b)
breadboards: 1

parts:
  Part1 = Arduino Uno (Rev3)
  LED3 = smd LED [color="Red (633nm)" package="0603 [SMD]"]

nets:
  N1: Part1.D11_PWM/MOSI, LED3.anode
  N2: Part1.GND, LED3.cathode
