# Fritzing sketch led-digits-clock-arduino (saved by Fritzing 0.9.1b)

parts:
  Part1 = Arduino Uno (Rev3)
  U2 = MAX7219 [package=dil24]

nets:
  N1: Part1.D2, U2.DIN
  N2: Part1.D3_PWM, U2.CS
  N3: Part1.D4, U2.CLK
  5V: Part1.5V, U2.VCC
  GND: Part1.GND, U2.GND

notes:
  Use with MAX7219 chip device

custom parts:
  MAX7219: 8-digit, 8-segment LED display driver, serial input
