# Fritzing sketch led-digits-clock-galileo (saved by Fritzing 0.9.1b)

parts:
  U2 = MAX7219 [package=dil24]
  Part2 = Intel Galileo Gen2

nets:
  N1: U2.DIN, Part2.D2
  N2: U2.CS, Part2.D3_PWM
  N3: U2.CLK, Part2.D4
  VCC: U2.VCC, Part2.5V
  GND: U2.GND, Part2.GND

notes:
  Use with MAX7219 chip device

custom parts:
  MAX7219: 8-digit, 8-segment LED display driver, serial input
