# Fritzing sketch led-matrix-HT16K33 (saved by Fritzing 0.9.0b)

parts:
  Part1 = Arduino Uno (Rev3)
  LED2 = 8x8 LED Matrix (yellow)
  LED3 = 8x8 LED Matrix (red)  # not connected
  LED4 = 8x8 LED Matrix (blue)  # not connected
  LED5 = 8x8 LED Matrix (green)  # not connected

nets:
  N1: Part1.A4/SDA, LED2.D
  N2: Part1.A5/SCL, LED2.C
  N3: Part1.5V, LED2.+
  N4: Part1.GND, LED2.-

custom parts:
  8x8 LED Matrix (yellow): 8x8 LED Matrix with I2C control (yellow)
  8x8 LED Matrix (red): 8x8 LED Matrix with I2C control (red)
  8x8 LED Matrix (blue): 8x8 LED Matrix with I2C control (blue)
  8x8 LED Matrix (green): 8x8 LED Matrix with I2C control (green)
