# Fritzing sketch led-matrix (saved by Fritzing 0.7.7b)
breadboards: 1

parts:
  MAX_7220 = MAX 7219 [package="DIP (Dual Inline) [THT]"]
  IC1 = IC, DIP package, 24 pins [chip_label="LED Matrix"]
  Arduino1 = Arduino
  R1 = Resistor [tolerance=±5% resistance=10k package=THT]

nets:
  N1: MAX_7220.DIN, Arduino1.D2
  N2: MAX_7220.DIG_0, IC1.pin22
  N3: MAX_7220.DIG_4, IC1.pin3
  GND: MAX_7220.GND, Arduino1.GND
  N4: MAX_7220.DIG_6, IC1.pin9
  N5: MAX_7220.DIG_2, IC1.pin16
  N6: MAX_7220.DIG_3, IC1.pin13
  N7: MAX_7220.DIG_7, IC1.pin12
  N8: MAX_7220.DIG_5, IC1.pin6
  N9: MAX_7220.DIG_1, IC1.pin19
  N10: MAX_7220.LOAD_(CS), Arduino1.D4
  N11: MAX_7220.CLK, Arduino1.D3
  N12: MAX_7220.SEG_A, IC1.pin21
  N13: MAX_7220.SEG_F, IC1.pin7
  N14: MAX_7220.SEG_B, IC1.pin18
  N15: MAX_7220.SEG_G, IC1.pin10
  N16: MAX_7220.ISET, R1.Pin_0
  N17: MAX_7220.V+, Arduino1.+5V, R1.Pin_1
  N18: MAX_7220.SEG_C, IC1.pin15
  N19: MAX_7220.SEG_E, IC1.pin4
  N20: MAX_7220.SEG_DP, IC1.pin24
  N21: MAX_7220.SEG_D, IC1.pin1

custom parts:
  MAX 7219: A led matrix driver on a 300 mil dual inline package (DIP) footprint.
