# Fritzing sketch led-rgb-PCA9685 (saved by Fritzing 0.9.1b)
breadboards: 1

parts:
  Part1 = Arduino Uno (Rev3)
  PWM1 = PCA9685 16x12-bit PWM Breakout
  LED1 = RGB LED (com. cathode, rgb) [package="5 mm [THT]"]

nets:
  N1: Part1.A4/SDA, PWM1.no_name_yet#504
  N2: Part1.A5/SCL, PWM1.no_name_yet#503
  N3: Part1.3V3, PWM1.no_name_yet#505
  N4: Part1.5V, PWM1.no_name_yet#506
  N5: Part1.GND, PWM1.no_name_yet#501, LED1.green_anode
  N6: PWM1.no_name_yet#0, LED1.blue_anode
  N7: PWM1.no_name_yet#1, LED1.common_cathode
  N8: PWM1.no_name_yet#2, LED1.red_anode
