# Fritzing sketch led-rgb-anode-PCA9685 (saved by Fritzing 0.9.2b)
breadboards: 1

parts:
  Part1 = Arduino Uno (Rev3)
  PWM1 = PCA9685 16x12-bit PWM Breakout
  LED2 = RGB LED (com. cathode, rgb) [package="5 mm [THT]"]
  R9 = Resistor [resistance=220 tolerance=±5% package=THT]
  R10 = Resistor [resistance=220 tolerance=±5% package=THT]
  R11 = Resistor [resistance=220 tolerance=±5% package=THT]

nets:
  N1: Part1.A4/SDA, PWM1.no_name_yet#504
  N2: Part1.A5/SCL, PWM1.no_name_yet#503
  N3: Part1.5V, PWM1.no_name_yet#505, PWM1.no_name_yet#506
  N4: Part1.GND, PWM1.no_name_yet#501, PWM1.no_name_yet#1002, LED2.common_cathode
  N5: PWM1.no_name_yet#0, R9.Pin_0
  N6: PWM1.no_name_yet#1, R10.Pin_0
  N7: PWM1.no_name_yet#2, R11.Pin_0
  N8: LED2.red_anode, R11.Pin_1
  N9: LED2.green_anode, R10.Pin_1
  N10: LED2.blue_anode, R9.Pin_1
