# Fritzing sketch led-rgb-anode (saved by Fritzing 0.9.1b)
breadboards: 1

parts:
  Part1 = Arduino Uno (Rev3)
  LED2 = RGB LED (com. anode, rbg) [package="5 mm [THT]"]
  R7 = Resistor [resistance=220 tolerance=±5% package=THT]
  R8 = Resistor [resistance=220 tolerance=±5% package=THT]
  R9 = Resistor [resistance=220 tolerance=±5% package=THT]

nets:
  N1: Part1.D9_PWM, R7.Pin_0
  N2: Part1.D10_PWM/SS, R8.Pin_0
  N3: Part1.D11_PWM/MOSI, R9.Pin_0
  N4: Part1.5V, LED2.blue_cathode
  N5: LED2.red_cathode, R9.Pin_1
  N6: LED2.common_anode, R8.Pin_1
  N7: LED2.green_cathode, R7.Pin_1
