# Fritzing sketch led-rgb (saved by Fritzing 0.8.7b)
breadboards: 1

parts:
  LED1 = RGB LED (com. anode, rbg) [package="5 mm [THT]"]
  Part1 = Arduino Uno (Rev3)
  LED2 = RGB LED (com. anode, rbg) [package="5 mm [THT]"]

nets:
  N1: LED1.red_cathode, Part1.D9_PWM
  N2: LED1.common_anode, Part1.GND, LED2.common_anode
  N3: LED1.blue_cathode, Part1.D10_PWM/SS
  N4: LED1.green_cathode, Part1.D11_PWM/MOSI
  N5: Part1.D3_PWM, LED2.red_cathode
  N6: Part1.D5_PWM, LED2.blue_cathode
  N7: Part1.D6_PWM, LED2.green_cathode
