# Fritzing sketch led-slider (saved by Fritzing 0.8.7b)
breadboards: 1

parts:
  Arduino3 = Arduino Uno (Rev3)
  U1 = SLIDER [package=slider]
  LED1 = LED - 5mm [color="Red (633nm)" package="5 mm [THT]"]

nets:
  N1: Arduino3.A0, U1.A
  N2: Arduino3.D11_PWM/MOSI, LED1.anode
  N3: Arduino3.GND, U1.E, LED1.cathode
  N4: Arduino3.5V, U1.S

custom parts:
  SLIDER: Slide-type potentiometer- COM-9119
