# Fritzing sketch light-ambient-BH1750-tessel (saved by Fritzing 0.9.3b)

parts:
  Part1 = BH1750
  Part3 = Tessel 2

nets:
  VCC: Part1.VCC, Part3.3V3
  GND: Part1.GND, Part3.GND
  N1: Part1.SCL, Part3.0
  N2: Part1.SDA, Part3.1

custom parts:
  BH1750: Light Sensor
  Tessel 2: Draft version of Tessel 2
