# Fritzing sketch light-ambient-TSL2561 (saved by Fritzing 0.9.1b)

parts:
  Part1 = Arduino Uno (Rev3)
  TSL1 = TSL2561

nets:
  N1: Part1.A4/SDA, TSL1.SDA
  N2: Part1.A5/SCL, TSL1.SCL
  5V: Part1.5V, TSL1.VIN
  GND: Part1.GND, TSL1.GND
