# Fritzing sketch microphone (saved by Fritzing 0.9.1b)

parts:
  Part2 = Breakout Board for Electret Microphone
  Part3 = Arduino Uno (Rev3)
  LED1 = LED - 3mm [color="Red (633nm)" package="3 mm [THT]"]

nets:
  VCC: Part2.VCC, Part3.5V
  GND: Part2.GND, Part3.GND, LED1.cathode
  N1: Part2.AUD, Part3.A0
  N2: Part3.D11_PWM/MOSI, LED1.anode
