# Fritzing sketch motion-gp2y0d805z0f (saved by Fritzing 0.9.1b)

parts:
  Part1 = Arduino Uno (Rev3)
  X1 = GP2Y0D805Z0F

nets:
  N1: Part1.A4/SDA, X1.SDA
  N2: Part1.A5/SCL, X1.SCL
  N3: Part1.5V, X1.+5
  GND: Part1.GND, X1.GND
