# Fritzing sketch motion-tessel (saved by Fritzing 0.9.1b)
breadboards: 1

parts:
  Part1 = Tessel 2
  LED1 = smd LED [color="Red (633nm)" package="0805 [SMD]"]
  PIR1 = PIR sensor

nets:
  N1: Part1.GND#28, LED1.cathode
  N2: Part1.2, PIR1.SIG
  N3: Part1.5, LED1.anode
  N4: Part1.GND#78, PIR1.GND
  5V: Part1.5V, PIR1.VDD

custom parts:
  Tessel 2: Draft version of Tessel 2
