# Fritzing sketch motor-3-pin (saved by Fritzing 0.8.5b)

parts:
  Arduino1 = Arduino Uno (Rev3)  # not connected
  M1 = DC Motor
  Part2 = Monster Moto Shield

nets:
  N1: M1.pin_1, Part2.OUTA1
  N2: M1.pin_2, Part2.OUTB1
