# Fritzing sketch motor-TB6612FNG (saved by Fritzing 0.9.3b)
breadboards: 1

parts:
  Part1 = Tessel 2
  PART1 = Motor Driver 1A Dual TB6612FNG [part_number=ROB_09457]  # not connected
  S2 = Toggle Switch [package=THT]
  R1 = TSR-3386UT Square Trimming Potentiometer [part_number=TSR-3386]
  Part2 = Dagu Gear Motor  # not connected
  Part3 = Dagu Gear Motor  # not connected

nets:
  N1: Part1.GND, S2.L2, R1.Leg2
  N2: Part1.3V3, S2.L1, R1.Leg1
  N3: Part1.0#30, S2.COM
  N4: Part1.0#40, R1.wiper

notes:
  Important: For this experiment, you'll need to use a USB wall wart to provide power. Motors are current-hungry—they’ll try to draw more current than a USB port can deliver. This will consistently cause the Tessel 2 to reboot and could potentially and permanently damage the board or your computer.

custom parts:
  Tessel 2: Draft version of Tessel 2
  Motor Driver 1A Dual TB6612FNG: The TB6612FNG motor driver can control up to two DC motors at a constant current of 1.2A (3.2A peak). Two input signals (IN1 and IN2) can be used to control the motor in one of four function modes - CW, CCW, short-brake, and stop. The two motor outputs (A and B) can be separately controlled, the speed of each motor is controlled via a PWM input signal with a frequency up to 100kHz. The STBY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
  TSR-3386UT Square Trimming Potentiometer: Trimpot 10K with Knob
  Dagu Gear Motor: The most common hobbyist/kit dc motor on the market in 2016
