# Fritzing sketch motor-current (saved by Fritzing 0.8.5b)

parts:
  M1 = DC Motor
  Arduino1 = Arduino Uno (Rev3)  # not connected
  Part1 = Arduino Motor Shield (Rev3)
  BAT1 = Battery Holders [package=battery-aa-kit]
  BAT2 = Battery Holders [package=battery-aa-kit]
  BAT4 = Battery Holders [package=battery-aa-kit]
  BAT5 = Battery Holders [package=battery-aa-kit]

nets:
  N1: M1.pin_1, Part1.A+
  N2: M1.pin_2, Part1.A-
  N3: Part1.VMOT, BAT5.-
  N4: Part1.GND, BAT1.+
  N5: BAT1.-, BAT4.+
  N6: BAT2.+, BAT4.-
  N7: BAT2.-, BAT5.+
