# Fritzing sketch motor-directional (saved by Fritzing 0.8.7b)

parts:
  M1 = DC Motor
  Part1 = Arduino Motor Shield
  Arduino1 = Arduino Uno (Rev3)  # not connected

nets:
  N1: M1.pin_1, Part1.OUT4
  N2: M1.pin_2, Part1.OUT3
