# Fritzing sketch motor-enable (saved by Fritzing 0.9.3b)
breadboards: 1

parts:
  M1 = DC Motor
  Arduino1 = Arduino Uno (Rev3)
  IC1 = H-Bridge [package=THT]
  BAT1 = Battery Holders [package=battery-aa-kit]
  BAT2 = Battery Holders [package=battery-aa-kit]
  BAT5 = Battery Holders [package=battery-aa-kit]
  BAT4 = Battery Holders [package=battery-aa-kit]

nets:
  N1: M1.pin_1, IC1.2Y
  N2: M1.pin_2, IC1.1Y
  N3: Arduino1.D12/MISO, IC1.1A
  GND: Arduino1.GND, IC1.GND1, IC1.GND2, IC1.GND3, IC1.GND4, BAT1.+
  N4: Arduino1.D3_PWM, IC1.2A
  N5: Arduino1.D7, IC1.1_2EN
  N6: Arduino1.5V, IC1.VCC1
  N7: IC1.VCC2, BAT5.-
  N8: BAT1.-, BAT4.+
  N9: BAT2.+, BAT4.-
  N10: BAT2.-, BAT5.+
