# Fritzing sketch motor-l298-breakout (saved by Fritzing 0.9.3b)

parts:
  Arduino1 = Arduino Uno (Rev3)
  S1 = H-Bridge with L298N
  M1 = DC Motor  # not connected
  BAT6 = Battery Holders [package=battery-aa-kit]
  BAT7 = Battery Holders [package=battery-aa-kit]
  BAT8 = Battery Holders [package=battery-aa-kit]
  BAT9 = Battery Holders [package=battery-aa-kit]

nets:
  N1: Arduino1.D8, S1.IN2
  N2: Arduino1.D9_PWM, S1.IN1
  GND: Arduino1.GND, S1.GND, BAT9.-
  N3: S1.12V, BAT6.+
  N4: BAT6.-, BAT8.+
  N5: BAT7.+, BAT8.-
  N6: BAT7.-, BAT9.+

custom parts:
  H-Bridge with L298N: h-bridge
