# Fritzing sketch motor-sparkfun-edison-hbridge (saved by Fritzing 0.9.1b)

parts:
  U1 = EDISON  # not connected
  sparkfun_intel_hbridge_block1 = SparkFun Intel HBridge Block
  M2 = DC Motor
  BATT1 = LiPoly Battery (1300mAh)

nets:
  N1: sparkfun_intel_hbridge_block1.VIN, BATT1.positive
  N2: sparkfun_intel_hbridge_block1.GND, BATT1.negative
  N3: sparkfun_intel_hbridge_block1.B1, M2.SIG
  N4: sparkfun_intel_hbridge_block1.B2, M2.GND

notes:
  The H-Bridge block is connected to the Edison via the Base Block

custom parts:
  DC Motor: Your standard DC Motor
  LiPoly Battery (1300mAh): Lithium Ion Polymer Battery (1300mAh)
