# Fritzing sketch multi-BME280-arduino (saved by Fritzing 0.9.2b)

parts:
  Part2 = Arduino Uno (Rev3) - ICSP
  Part4 = Adafruit BME280

nets:
  N1: Part2.A4/SDA, Part4.SDI/SDA
  N2: Part2.A5/SCL, Part4.SCK/SCL
  5V: Part2.5V, Part4.VIN
  GND: Part2.GND, Part4.GND

custom parts:
  Adafruit BME280: Bosch has stepped up their game with their new BME280 sensor, an environmental sensor with temperature, barometric pressure and humidity! This sensor is great for all sorts of weather/environmental sensing and can even be used in both I2C and SPI! This precision sensor from Bosch is the best low-cost sensing solution for measuring humidity with ±3% accuracy, barometric pressure with ±1 hPa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
