# Fritzing sketch multi-DHT11_I2C_NANO_BACKPACK (saved by Fritzing 0.9.1b)

parts:
  DHT1 = DHT11 Humitidy and Temperature Sensor
  Part1 = Arduino Nano (Rev3.0) (ICSP)
  Part2 = Arduino Uno (Rev3) - ICSP
  R2 = Resistor [tolerance=±5% resistance=10k package="1206 [SMD]"]

nets:
  VDD: DHT1.VDD, Part1.5V, R2.Pin_1
  N1: DHT1.DATA, Part1.D2
  GND: DHT1.GND, Part1.GND, Part2.GND
  VIN: Part1.VIN, Part2.5V
  N2: Part1.A5, Part2.A5/SCL
  N3: Part1.A4, Part2.A4/SDA

custom parts:
  DHT11 Humitidy and Temperature Sensor: DHT11 Humidity and Temperature Sensor
