# Fritzing sketch multi-DHT21_I2C_NANO_BACKPACK (saved by Fritzing 0.9.3b)

parts:
  Part1 = Arduino Nano (Rev3.0) (ICSP)
  Part2 = Arduino Uno (Rev3) - ICSP
  R2 = Resistor [tolerance=±5% resistance=10k package="1206 [SMD]"]
  DHT2 = DHT22/AM2301 Humidity and Temperature Sensor

nets:
  N1: Part1.D2, DHT2.DATA
  VIN: Part1.VIN, Part2.5V
  GND: Part1.GND, Part2.GND, DHT2.GND
  5V: Part1.5V, R2.Pin_1, DHT2.VDD
  N2: Part1.A5, Part2.A5/SCL
  N3: Part1.A4, Part2.A4/SDA
