# Fritzing sketch multi-HIH6130 (saved by Fritzing 0.9.2b)

parts:
  Part2 = Arduino Uno (Rev3) - ICSP
  Part3 = SparkFun Humidity and Temperature Sensor Breakout - HIH6130

nets:
  N1: Part2.A4/SDA, Part3.SDA
  N2: Part2.A5/SCL, Part3.SCL
  5V: Part2.5V, Part3.VDD
  GND: Part2.GND, Part3.GND

custom parts:
  SparkFun Humidity and Temperature Sensor Breakout - HIH6130: The HIH6130 is a digital output-type relative humidity (RH) and temperature sensor combined in the same package. This allows the RH measurement to be temperature compensated and provides a second, standalone temperature sensor output.
