# Fritzing sketch multi-MS5611 (saved by Fritzing 0.9.1b)

parts:
  BMP1 = MS5611
  Part1 = Arduino Uno (Rev3)

nets:
  VIN: BMP1.VIN, Part1.5V
  N1: BMP1.SCL, Part1.A5/SCL
  N2: BMP1.SDA, Part1.A4/SDA
  GND: BMP1.GND, Part1.GND
