# Fritzing sketch multi-SI7021-uno (saved by Fritzing 0.9.3b)

parts:
  SI1 = SI7021
  Part2 = Arduino Uno (Rev3)

nets:
  N1: SI1.3Vo, Part2.3V3
  N2: SI1.SCL, Part2.A5/SCL
  N3: SI1.SDA, Part2.A4/SDA
  GND: SI1.GND, Part2.GND
