# Fritzing sketch multi-SI7021 (saved by Fritzing 0.9.3b)

parts:
  Part1 = Tessel 2
  SI1 = SI7021

nets:
  GND: Part1.GND, SI1.GND
  N1: Part1.3V3, SI1.3Vo
  N2: Part1.0, SI1.SCL
  N3: Part1.1, SI1.SDA

custom parts:
  Tessel 2: Draft version of Tessel 2
