# Fritzing sketch multi-TH02 (saved by Fritzing 0.9.1b)

parts:
  Grove3 = Grove 4 Digit Display
  Part1 = Base Shield V2

nets:
  N1: Grove3.GND, Part1.pin_124
  N2: Grove3.VCC, Part1.pin_125
  N3: Grove3.SDA, Part1.pin_126
  N4: Grove3.SCL, Part1.pin_127

custom parts:
  Grove 4 Digit Display: A 4 7-seg display
