# Fritzing sketch multi-bmp085-sfe (saved by Fritzing 0.9.1b)

parts:
  Part1 = Arduino Uno (Rev3)
  Part3 = Barometric Pressure Sensor - BMP085 Breakout

nets:
  N1: Part1.A4/SDA, Part3.SDA
  N2: Part1.A5/SCL, Part3.SCL
  5V: Part1.5V, Part3.VCC
  GND: Part1.GND, Part3.GND
