# Fritzing sketch multi-bmp085 (saved by Fritzing 0.9.1b)

parts:
  Part1 = Arduino Uno (Rev3)
  BMP2 = BMP085 Breakout

nets:
  N1: Part1.A4/SDA, BMP2.SDA
  N2: Part1.A5/SCL, BMP2.SCL
  5V: Part1.5V, BMP2.VIN
  GND: Part1.GND, BMP2.GND

custom parts:
  BMP085 Breakout: A breakout for the BMP085 barometric pressure and temperature sensor
