# Fritzing sketch multi-bmp180-sfe (saved by Fritzing 0.9.3b)

parts:
  Part1 = Arduino Uno (Rev3)
  Part2 = BMP180 Breakout [part_number=SEN-11824]

nets:
  N1: Part1.A4/SDA, Part2.SDA
  N2: Part1.A5/SCL, Part2.SCL
  3V3: Part1.3V3, Part2.3.3V
  GND: Part1.GND, Part2.GND

custom parts:
  BMP180 Breakout: This is a breadboard friendly breakout board for the BMP180 high-precision, temp and pressure sensor.
