# Fritzing sketch multi-mpl115a2 (saved by Fritzing 0.9.0b)

parts:
  SENSOR1 = MPL115A2 Barometer Breakout Board
  Part1 = Arduino Uno (Rev3)

nets:
  N1: SENSOR1.SDA, Part1.A4/SDA
  N2: SENSOR1.SCL, Part1.A5/SCL
  GND: SENSOR1.GND, Part1.GND
  VDD: SENSOR1.VDD, Part1.5V

custom parts:
  MPL115A2 Barometer Breakout Board: MPL115A2 I2C Barometric Sensor
