# Fritzing sketch navigator-joystick (saved by Fritzing 0.7.1b)

parts:
  Arduino4 = Arduino
  Arduino5 = Arduino
  Part2 = Thumb Joystick
  J2 = Basic Servo
  LED2 = LED - 5mm [color="Red (633nm)" package="5 mm [THT]"]

nets:
  +5V: Arduino4.+5V, Part2.VCC
  GND: Arduino4.GND, Part2.GND
  N1: Arduino4.A0, Part2.VERT
  N2: Arduino4.A1, Part2.HORZ
  GND_2: Arduino5.GND, J2.gnd, LED2.cathode
  N3: Arduino5.D13, LED2.anode
  N4: Arduino5.D9, J2.pulse
  +5V_2: Arduino5.+5V, J2.vcc

notes:
  navigator
  controller
