# Fritzing sketch photoresistor (saved by Fritzing 0.8.7b)
breadboards: 1

parts:
  R1 = Photocell (LDR) [package=THT]
  R2 = Resistor [tolerance=±5% resistance=10k package=THT]
  Arduino1 = Arduino Uno (Rev3)

nets:
  N1: R1.pin_0, R2.Pin_1, Arduino1.A2
  N2: R1.pin_1, Arduino1.GND
