# Fritzing sketch ping (saved by Fritzing 0.7.7b)
breadboards: 1

parts:
  Arduino1 = Arduino
  J1 = Infrared Proximity Sensor

nets:
  N1: Arduino1.D7, J1.Vout
  +5V: Arduino1.+5V, J1.Vcc
  GND: Arduino1.GND, J1.GND
