# Fritzing sketch potentiometer (saved by Fritzing 0.8.7b)
breadboards: 1

parts:
  R1 = Rotary Potentiometer (Large) [maximum_resistance=100kΩ package=THT]
  part = Rotary Potentiometer (Large) [maximum_resistance=100kΩ package=THT]  # not connected
  Arduino2 = Arduino Uno (Rev3)

nets:
  N1: R1.leg1, Arduino2.GND
  N2: R1.wiper, Arduino2.A3
