# Fritzing sketch proximity-collection-HCSR04_I2C_BACKPACK-tessel (saved by Fritzing 0.9.2b)

parts:
  Part1 = Tessel 2
  Part2 = Arduino Nano (Rev3.0) (ICSP)
  Part3 = SRF05 Ultrasonic Rangefinder
  Part4 = SRF05 Ultrasonic Rangefinder
  Part5 = SRF05 Ultrasonic Rangefinder
  Part6 = SRF05 Ultrasonic Rangefinder

nets:
  N1: Part1.0, Part2.A5
  N2: Part1.1, Part2.A4
  GND: Part1.GND, Part2.GND
  5V: Part1.5V, Part2.VIN
  N3: Part2.D6, Part3.Trig, Part3.Echo
  N4: Part2.D7, Part4.Trig, Part4.Echo
  N5: Part2.D8, Part5.Trig, Part5.Echo
  N6: Part2.D9, Part6.Trig, Part6.Echo

notes:
  To keep this diagram uncluttered, the VCC & Ground wiring for the sensors is omitted. For the circuit to work properly, you must:
  - Connect all of the VCC pins to 5V
  - Connect all of the GND pins to Gound

custom parts:
  Tessel 2: Draft version of Tessel 2
