# Fritzing sketch proximity-hcsr04-i2c (saved by Fritzing 0.9.3b)

parts:
  Part1 = Arduino Nano (Rev3.0)
  Part2 = SRF05 Ultrasonic Rangefinder
  Part3 = Arduino Uno (Rev3)

nets:
  GND: Part1.GND, Part2.GND, Part3.GND
  N1: Part1.D8, Part2.Trig, Part2.Echo
  VIN: Part1.VIN, Part3.5V
  5V: Part1.5V, Part2.VCC
  N2: Part1.A5, Part3.A5/SCL
  N3: Part1.A4, Part3.A4/SDA
