# Fritzing sketch proximity-lidarlite (saved by Fritzing 0.9.1b)

parts:
  Part1 = LIDAR-Lite
  Part2 = Arduino Uno (Rev3)
  A1 = Power Source [package=power_jack_combo]

nets:
  N1: Part1.5V, A1.PWR1
  N2: Part1.SCL, Part2.A5/SCL
  N3: Part1.SDA, Part2.A4/SDA
  GND: Part1.GND, Part2.GND, A1.GND1

notes:
  Requires an external power source. 4.7 - 5.5V DC Nominal, Maximum 6V DC

custom parts:
  LIDAR-Lite: PulsedLight LIDAR-Lite Sensor
