# Fritzing sketch proximity-mb1003 (saved by Fritzing 0.9.2b)

parts:
  Part1 = Arduino Uno (Rev3)
  SONAR1 = Maxbotix MaxSonar Ultrasonic Sensor

nets:
  N1: Part1.A0, SONAR1.AN
  5V: Part1.5V, SONAR1.+5V
  GND: Part1.GND, SONAR1.GND

custom parts:
  Maxbotix MaxSonar Ultrasonic Sensor: Maxbotix MaxSonar Ultrasonic Sensor LV-EZ0, LV-EZ1, LV-EZ2, LV-EZ3, LV-EZ4
