# Fritzing sketch proximity-srf10 (saved by Fritzing 0.9.2b)

parts:
  X1 = Sonar
  Part1 = Arduino Uno (Rev3)

nets:
  N1: X1.+5, Part1.5V
  N2: X1.SDA, Part1.A4/SDA
  N3: X1.SCL, Part1.A5/SCL
  GND: X1.GND, Part1.GND

custom parts:
  Sonar: Devantech SRF08 sonar range-finder. I2C interface. Other Devantech sonars similar
