# Fritzing sketch relay-collection (saved by Fritzing 0.9.1b)
stripboards: 1

parts:
  KY-1 = Keyes Relay [package=THT]
  KY-2 = Keyes Relay [package=THT]
  KY-3 = Keyes Relay [package=THT]
  Part1 = Arduino Uno (Rev3)

nets:
  N1: KY-1.signal, Part1.D3_PWM
  N2: KY-1.power, KY-2.power, KY-3.power, Part1.5V
  N3: KY-1.ground, KY-2.ground, KY-3.ground, Part1.GND
  N4: KY-2.signal, Part1.D4
  N5: KY-3.signal, Part1.D5_PWM

custom parts:
  Keyes Relay: The Keyes 5V relay module is suitable for SCM development, home appliance control. It uses a 5V~12V TIL control signal which can control DC / AC signal.
