# Fritzing sketch relay (saved by Fritzing 0.8.5b)
breadboards: 1

parts:
  Part1 = Arduino Uno (Rev3)
  Q1 = TRANSISTOR_NPN [package=to-92-ammo]
  Part2 = songle relay
  R1 = Resistor [tolerance=±5% resistance=220 package=THT]
  LED1 = LED - 5mm [color="Red (633nm)" package="5 mm [THT]"]

nets:
  N1: Part1.D10_PWM/SS, Q1.B
  N2: Part1.GND, Q1.E, LED1.anode
  N3: Part1.5V, Part2.COIL2
  N4: R1.Pin_1, LED1.cathode
