# Fritzing sketch sensor-digital-microwave (saved by Fritzing 0.9.3b)

parts:
  Microwave_Sensor1 = DFRobot Microwave Sensor
  Part1 = Arduino Uno (Rev3)

nets:
  N1: Microwave_Sensor1.SIG, Part1.D7
  GND: Microwave_Sensor1.GND, Part1.GND
  VCC: Microwave_Sensor1.VCC, Part1.5V

custom parts:
  DFRobot Microwave Sensor: https://www.dfrobot.com/wiki/index.php/MicroWave_Sensor_SKU:_SEN0192
