# Fritzing sketch sensor-temperature-tmp36 (saved by Fritzing 0.8.7b)
breadboards: 1

parts:
  Part1 = Arduino Uno (Rev3)
  U1 = TMP36 [package=to-92-kit]

nets:
  N1: Part1.A0, U1.VOUT
  5V: Part1.5V, U1.VCC
  GND: Part1.GND, U1.GND

notes:
  Flat side of sensor should be toward the Arduino.
