# Fritzing sketch servo-PCA9685 (saved by Fritzing 0.9.0b)

parts:
  Part1 = Arduino Uno (Rev3)
  Part2 = Servo Improved
  Part3 = 16-Channel 12-bit PCA9685 PWM/Servo Driver
  J1 = Screw terminal - 2 pins [package=THT]
  Power_plug1 = Power plug

nets:
  N1: Part1.A4/SDA, Part3.SDA
  N2: Part1.A5/SCL, Part3.SCL
  5V: Part1.5V, Part3.VCC
  GND: Part1.GND, Part2.ground, Part3.GND, J1.pin2, Power_plug1.GND
  N3: Part2.vcc, Part3.V+
  N4: Part2.signal, Part3.0
  N5: Part3.PWRIN, J1.pin1, Power_plug1.VCC

custom parts:
  16-Channel 12-bit PCA9685 PWM/Servo Driver: The Adafruit 16-Channel 12-bit PWM/Servo Driver will drive up to 16 servos over I2C with only 2 pins. The on-board PCA9685 PWM controller will drive all 16 channels simultaneously with no additional processing overhead. What's more, you can chain up to 62 of them to control up to 992 servos - all with the same 2 pins
