# Fritzing sketch servo-continuous (saved by Fritzing 0.8.7b)

parts:
  Part1 = Arduino Uno (Rev3)
  Part2 = Servo Improved

nets:
  N1: Part1.D10_PWM/SS, Part2.signal
  5V: Part1.5V, Part2.vcc
  N2: Part1.GND, Part2.ground
