# Fritzing sketch servo-diagnostic (saved by Fritzing 0.8.7b)
breadboards: 1

parts:
  Arduino3 = Arduino Uno (Rev3)
  Part3 = Servo Improved
  Part4 = Breadboard Power Supply Board SMD
  Part5 = Servo Improved

nets:
  N1: Arduino3.D9_PWM, Part5.signal
  N2: Arduino3.D10_PWM/SS, Part3.signal
  GND: Arduino3.GND, Part3.ground, Part4.GND, Part5.ground
  VCC: Part3.vcc, Part4.VCC, Part5.vcc

notes:
  Substitute with your own power source
