# Fritzing sketch servo-drive (saved by Fritzing 0.8.7b)
breadboards: 1

parts:
  Arduino2 = Arduino Uno (Rev3)
  VCC1 = 4 x AAA Battery Mount
  J1 = Basic Servo
  J2 = Basic Servo

nets:
  N1: Arduino2.D9_PWM, J2.pulse
  N2: Arduino2.D10_PWM/SS, J1.pulse
  GND: Arduino2.GND, VCC1.-, J1.gnd, J2.gnd
  VCC: VCC1.+, J1.vcc, J2.vcc
