# Fritzing sketch servo-keypress (saved by Fritzing 0.8.7b)
breadboards: 1

parts:
  Arduino2 = Arduino Uno (Rev3)
  VCC1 = 4 x AAA Battery Mount
  J1 = Basic Servo

nets:
  N1: Arduino2.D10_PWM/SS, J1.pulse
  GND: Arduino2.GND, VCC1.-, J1.gnd
  N2: VCC1.+, J1.vcc
