# Fritzing sketch servo-slider (saved by Fritzing 0.9.0b)
breadboards: 1

parts:
  Arduino3 = Arduino Uno (Rev3)
  U2 = SLIDER [package=slider]
  Part3 = Servo Improved
  Part4 = Breadboard Power Supply Board SMD

nets:
  N1: Arduino3.A0, U2.E
  N2: Arduino3.D10_PWM/SS, Part3.signal
  GND: Arduino3.GND, U2.S, Part3.ground, Part4.GND
  VCC: U2.A, Part3.vcc, Part4.VCC
