# Fritzing sketch servo-sweep (saved by Fritzing 0.8.7b)

parts:
  J1 = Basic Servo
  Arduino2 = Arduino Uno (Rev3)

nets:
  GND: J1.gnd, Arduino2.GND
  VCC: J1.vcc, Arduino2.5V
  N1: J1.pulse, Arduino2.D10_PWM/SS
