# Fritzing sketch servos-two-controllers (saved by Fritzing 0.9.2b)
breadboards: 1

parts:
  Part1 = Arduino Uno (Rev3)
  Part2 = Servo Improved
  BAT6 = Battery Holders [package=battery-aa-kit]
  BAT7 = Battery Holders [package=battery-aa-kit]
  BAT8 = Battery Holders [package=battery-aa-kit]
  BAT9 = Battery Holders [package=battery-aa-kit]
  Part3 = Servo Improved
  PWM2 = PCA9685 16x12-bit PWM Breakout

nets:
  N1: Part1.A4/SDA, PWM2.no_name_yet#604
  N2: Part1.A5/SCL, PWM2.no_name_yet#603
  N3: Part1.D10_PWM/SS, Part2.signal
  N4: Part1.GND, Part2.ground, BAT9.+, Part3.ground, PWM2.no_name_yet#701, PWM2.no_name_yet#1000
  VCC: Part2.vcc, BAT6.-, Part3.vcc, PWM2.no_name_yet#100, PWM2.no_name_yet#706
  N5: BAT6.+, BAT8.-
  N6: BAT7.+, BAT9.-
  N7: Part3.signal, PWM2.no_name_yet#0
