# Fritzing sketch servos (saved by Fritzing 0.9.2b)
breadboards: 1

parts:
  Part1 = Arduino Uno (Rev3)
  Part2 = Servo Improved
  BAT6 = Battery Holders [package=battery-aa-kit]
  BAT7 = Battery Holders [package=battery-aa-kit]
  BAT8 = Battery Holders [package=battery-aa-kit]
  BAT9 = Battery Holders [package=battery-aa-kit]
  Part3 = Servo Improved

nets:
  N1: Part1.D9_PWM, Part3.signal
  N2: Part1.D10_PWM/SS, Part2.signal
  N3: Part1.GND, Part2.ground, BAT9.+, Part3.ground
  VCC: Part2.vcc, BAT6.-, Part3.vcc
  N4: BAT6.+, BAT8.-
  N5: BAT7.+, BAT9.-
