# Fritzing sketch seven-segment (saved by Fritzing 0.7.7b)
breadboards: 1

parts:
  Arduino1 = Arduino
  U1 = 74HC595 [package="DIP16 [THT]"]
  DI1 = 7-Segment LED Display [package=THT]
  R1 = Resistor [tolerance=±5% resistance=330 package=THT]

nets:
  N1: Arduino1.D4, U1.ST_CP
  N2: Arduino1.D3, U1.SH_CP
  N3: Arduino1.D2, U1.DS
  +5V: Arduino1.+5V, U1.MR, U1.VCC, R1.Pin_1
  GND: Arduino1.GND, U1.GND, U1.OE
  N4: U1.Q1, DI1.cathodeB
  N5: U1.Q2, DI1.cathodeC
  N6: U1.Q3, DI1.cathodeD
  N7: U1.Q4, DI1.cathodeE
  N8: U1.Q5, DI1.cathodeF
  N9: U1.Q6, DI1.cathodeG
  N10: U1.Q7, DI1.cathodeDP
  N11: U1.Q0, DI1.cathodeA
  N12: DI1.commAnode#7, R1.Pin_0
