# Fritzing sketch shift-register-daisy-chain-anode (saved by Fritzing 0.9.1b)
breadboards: 1

parts:
  ARD = Arduino Uno (Rev3)
  DI2 = 7-Segment LED Display [package=THT]
  U1 = 74HC595 [package="DIP16 [THT]"]
  U2 = 74HC595 [package="DIP16 [THT]"]
  DI3 = 7-Segment LED Display [package=THT]
  R1 = Resistor [tolerance=±5% resistance=220 package="0603 [SMD]"]
  R2 = Resistor [tolerance=±5% resistance=220 package="0603 [SMD]"]
  DigitalPushButtonV1 = Button Breakout

nets:
  N1: ARD.D8, DigitalPushButtonV1.Signal
  N2: ARD.D9_PWM, U1.MR, U2.MR
  N3: ARD.D2, U1.DS
  N4: ARD.D3_PWM, U1.ST_CP, U2.ST_CP
  N5: ARD.D4, U1.SH_CP, U2.SH_CP
  N6: DI2.cathodeE, U2.Q4
  N7: DI2.cathodeD, U2.Q3
  N8: DI2.commAnode#2, R1.Pin_1
  N9: DI2.cathodeC, U2.Q2
  N10: DI2.cathodeB, U2.Q1
  N11: DI2.cathodeA, U2.Q0
  N12: DI2.cathodeF, U2.Q5
  N13: DI2.cathodeG, U2.Q6
  N14: U1.Q1, DI3.cathodeB
  N15: U1.Q2, DI3.cathodeC
  N16: U1.Q3, DI3.cathodeD
  N17: U1.Q4, DI3.cathodeE
  N18: U1.Q5, DI3.cathodeF
  N19: U1.Q6, DI3.cathodeG
  GND: U1.GND, U1.OE, U2.GND, U2.OE, DigitalPushButtonV1.GND
  N20: U1.Q7', U2.DS
  N21: U1.Q0, DI3.cathodeA
  VCC: U1.VCC, U2.VCC, R1.Pin_0, R2.Pin_0, DigitalPushButtonV1.Input
  N22: DI3.commAnode#2, R2.Pin_1

notes:
  These are common anode displays.
  A - Orange
  B - Yellow
  C - Green
  D - Blue
  E - Cyan
  F - Purple
  G - Pink
  DP - N/C (Can be connected if necessary)
