# Fritzing sketch shift-register-daisy-chain (saved by Fritzing 0.9.1b)
breadboards: 3

parts:
  IC2 = 74HC595 SMD [package="SO16 [SMD]"]
  IC1 = 74HC595 SMD [package="SO16 [SMD]"]
  ARD = Arduino Uno (Rev3)
  CATHODE2 = 7 Segment Display
  CATHODE1 = 7 Segment Display
  R3 = Resistor [tolerance=±5% resistance=330 package=THT]
  R5 = Resistor [tolerance=±5% resistance=330 package=THT]
  R1 = Resistor [tolerance=±5% resistance=330 package=THT]
  R2 = Resistor [tolerance=±5% resistance=330 package=THT]
  R4 = Resistor [tolerance=±5% resistance=330 package=THT]
  R6 = Resistor [tolerance=±5% resistance=330 package=THT]
  R7 = Resistor [tolerance=±5% resistance=330 package=THT]
  R8 = Resistor [tolerance=±5% resistance=330 package=THT]
  R9 = Resistor [tolerance=±5% resistance=330 package=THT]
  R10 = Resistor [tolerance=±5% resistance=330 package=THT]
  R11 = Resistor [tolerance=±5% resistance=330 package=THT]
  R12 = Resistor [tolerance=±5% resistance=330 package=THT]
  R14 = Resistor [tolerance=±5% resistance=330 package=THT]
  R15 = Resistor [tolerance=±5% resistance=10k package=THT]
  R13 = Resistor [tolerance=±5% resistance=330 package=THT]
  S1 = Pushbutton [package="[THT]"]

nets:
  N1: IC2.Q1, R13.Pin_1
  N2: IC2.Q2, R14.Pin_1
  N3: IC2.Q3, R8.Pin_1
  N4: IC2.Q4, R9.Pin_1
  N5: IC2.Q5, R10.Pin_1
  N6: IC2.Q6, R11.Pin_1
  GND: IC2.GND, IC2.OE, IC1.GND, IC1.OE, ARD.GND, CATHODE2.common_cathode, CATHODE1.common_cathode, S1.Pin_1, S1.Pin_2
  N7: IC2.MR, IC1.MR, ARD.D7
  N8: IC2.SH_CP, IC1.SH_CP, ARD.D3_PWM
  N9: IC2.ST_CP, IC1.ST_CP, ARD.D4
  N10: IC2.DS, IC1.Q7'
  N11: IC2.Q0, R12.Pin_1
  VCC: IC2.VCC, IC1.VCC, ARD.5V, R15.Pin_1
  N12: IC1.Q1, R2.Pin_1
  N13: IC1.Q2, R3.Pin_1
  N14: IC1.Q3, R4.Pin_1
  N15: IC1.Q4, R5.Pin_1
  N16: IC1.Q5, R6.Pin_1
  N17: IC1.Q6, R7.Pin_1
  N18: IC1.DS, ARD.D2
  N19: IC1.Q0, R1.Pin_1
  N20: ARD.D8, R15.Pin_0, S1.Pin_3, S1.Pin_4
  N21: CATHODE2.Segment_A#1, R10.Pin_0
  N22: CATHODE2.Segment_F, R11.Pin_0
  N23: CATHODE2.Segment_E, R9.Pin_0
  N24: CATHODE2.Segment_D, R8.Pin_0
  N25: CATHODE2.Segment_C, R14.Pin_0
  N26: CATHODE2.Segment_B, R13.Pin_0
  N27: CATHODE2.Segment_A#10, R12.Pin_0
  N28: CATHODE1.Segment_A#1, R6.Pin_0
  N29: CATHODE1.Segment_F, R7.Pin_0
  N30: CATHODE1.Segment_E, R5.Pin_0
  N31: CATHODE1.Segment_D, R4.Pin_0
  N32: CATHODE1.Segment_C, R3.Pin_0
  N33: CATHODE1.Segment_B, R2.Pin_0
  N34: CATHODE1.Segment_A#10, R1.Pin_0

notes:
  If you choose not to connect ARD pin 9 to MR of IC2, you should replace it with VCC
  These are common cathode displays.
