# Fritzing sketch shift-register-seven-segment-anode (saved by Fritzing 0.9.1b)
breadboards: 1

parts:
  ARD = Arduino Uno (Rev3)
  U1 = 74HC595 [package="DIP16 [THT]"]
  DI3 = 7-Segment LED Display [package=THT]
  R2 = Resistor [tolerance=±5% resistance=220 package="0603 [SMD]"]

nets:
  N1: ARD.D9_PWM, U1.MR
  N2: ARD.D2, U1.DS
  N3: ARD.D3_PWM, U1.ST_CP
  N4: ARD.D4, U1.SH_CP
  N5: U1.Q1, DI3.cathodeB
  N6: U1.Q2, DI3.cathodeC
  N7: U1.Q3, DI3.cathodeD
  N8: U1.Q4, DI3.cathodeE
  N9: U1.Q5, DI3.cathodeF
  N10: U1.Q6, DI3.cathodeG
  N11: U1.Q7, DI3.cathodeDP
  N12: U1.GND, U1.OE
  N13: U1.Q0, DI3.cathodeA
  N14: U1.VCC, R2.Pin_0
  N15: DI3.commAnode#2, R2.Pin_1

notes:
  This is a common anode display.
  A - Orange
  B - Yellow
  C - Green
  D - Blue
  E - Cyan
  F - Purple
  G - Pink
  DP - Brown
