# Fritzing sketch slider-pan (saved by Fritzing 0.7.1b)
breadboards: 1

parts:
  J1 = Basic Servo
  R1 = Slide Potentiometer [maximum_resistance=100kΩ]
  Arduino1 = Arduino

nets:
  GND: J1.gnd, R1.wiper, Arduino1.GND
  VCC: J1.vcc, R1.leg2, Arduino1.+5V
  N1: R1.leg1, Arduino1.A0
