# Fritzing sketch sonar (saved by Fritzing 0.7.1b)
breadboards: 1

parts:
  Arduino1 = Arduino
  J1 = Infrared Proximity Sensor

nets:
  +5V: Arduino1.+5V, J1.Vcc
  GND: Arduino1.GND, J1.GND
  N1: Arduino1.A2, J1.Vout
