# Fritzing sketch stepper-driver (saved by Fritzing 0.8.0b)
breadboards: 1

parts:
  Part1 = Arduino Uno (Rev3)
  DRV1 = A4983
  M1 = Stepper Motor - Bipolar
  C1 = Electrolytic Capacitor [capacitance=100µF voltage=35V package="200 mil [THT, electrolytic]"]

nets:
  N1: Part1.ICSP_MISO, Part1.D12/MISO, DRV1.DIR
  N2: Part1.ICSP_SCK, Part1.D13/SCK, DRV1.STEP
  GND: Part1.GND, DRV1.GND
  5V: Part1.5V, DRV1.RST, DRV1.VDD
  N3: DRV1.VMOT, C1.+
  N4: DRV1.GNDMOT, C1.-
  N5: DRV1.2B, M1.A
  N6: DRV1.2A, M1.C
  N7: DRV1.1A, M1.B
  N8: DRV1.1B, M1.D

notes:
  Motor Power

custom parts:
  A4983: Poloko A4983 Stepper Motor Control Breakout
