# Fritzing sketch stepper-easy-driver (saved by Fritzing 0.9.1b)

parts:
  Part1 = EasyDriver_v44
  Part2 = Arduino Uno (Rev3)
  M1 = Stepper Motor - Bipolar
  A1 = Power Source [package=power_jack_combo]

nets:
  GND: Part1.GND, Part2.GND, A1.GND3
  N1: Part1.V+, A1.PWR3
  N2: Part1.STEP, Part2.D3_PWM
  N3: Part1.DIR, Part2.D2
  N4: Part1.OUT2A, M1.A
  N5: Part1.OUT2B, M1.C
  N6: Part1.OUT1A, M1.B
  N7: Part1.OUT1B, M1.D

notes:
  Steppers require an external power source.
