# Fritzing sketch stepper-four_wire (saved by Fritzing 0.8.0b)
breadboards: 1

parts:
  Part1 = Arduino Uno (Rev3)
  M1 = Stepper Motor - Bipolar
  IC1 = L293D [package=THT]

nets:
  N1: Part1.ICSP_MOSI, Part1.D11_PWM/MOSI, IC1.In_2
  N2: Part1.GND, IC1.0V
  N3: Part1.D10_PWM/SS, IC1.In_1
  N4: Part1.D12/MISO, IC1.In_3
  N5: Part1.D13/SCK, IC1.In_4
  N6: Part1.5V, IC1.Enable_1, IC1.Enable_2, IC1.+V
  N7: M1.A, IC1.Out_4_(_Controlled_by_Enable_2_)
  N8: M1.C, IC1.Out_3_(_Controlled_by_Enable_2_)
  N9: M1.B, IC1.Out_2_(_Controlled_by_Enable_1_)
  N10: M1.D, IC1.Out_1_(_Controlled_by_Enable_1_)

notes:
  Motor Power
