# Fritzing sketch switch-magnetic-door-tessel (saved by Fritzing 0.9.1b)

parts:
  S3 = Magnetic Door Switch [package=reed_switch_plastic]
  Part2 = Tessel 2

nets:
  N1: S3.1, Part2.GND
  N2: S3.2, Part2.3

custom parts:
  Tessel 2: Draft version of Tessel 2
