# Fritzing sketch switch-magnetic-door (saved by Fritzing 0.9.1b)

parts:
  S3 = Magnetic Door Switch [package=reed_switch_plastic]
  Part1 = Arduino Uno (Rev3)

nets:
  N1: S3.1, Part1.GND
  N2: S3.2, Part1.D7
