# Fritzing sketch switch-spst-rocker (saved by Fritzing 0.9.1b)
breadboards: 1

parts:
  Part1 = Arduino Uno (Rev3)
  U4 = SWITCH-SPST-2 [package=switch-spst-vertical]
  R1 = Resistor [tolerance=±5% package="2010 [SMD]"]

nets:
  N1: Part1.D8, U4.O, R1.Pin_1
  N2: Part1.5V, U4.P
  N3: Part1.GND, R1.Pin_0
