# Fritzing sketch switch-tilt-SW_200D (saved by Fritzing 0.9.0b)
breadboards: 1

parts:
  S1 = TILT-SWITCH-SW-200D [package=reed_switch_plastic]
  R1 = Resistor [tolerance=±5% resistance=220 package=THT]
  Part1 = Arduino Uno (Rev3) - ICSP

nets:
  N1: S1.1, Part1.5V
  N2: R1.Pin_0, Part1.D2
  N3: R1.Pin_1, Part1.GND
