# Fritzing sketch temperature-HTU21D-F (saved by Fritzing 0.9.1b)

parts:
  Part1 = HTU21D Breakout
  Part3 = Arduino Uno (Rev3)

nets:
  N1: Part1.SCL, Part3.A5/SCL
  N2: Part1.SDA, Part3.A4/SDA
  GND: Part1.GND, Part3.GND
  VIN: Part1.VIN, Part3.5V

custom parts:
  HTU21D Breakout: This is a breadboard friendly breakout board for the Measurement Specialties high-precision, low-power digital humidity sensor.
