# Fritzing sketch temperature-HTU21D (saved by Fritzing 0.9.1b)

parts:
  Part1 = Tessel 2
  Part2 = HTU21D Breakout

nets:
  GND: Part1.GND, Part2.GND
  3V3: Part1.3V3, Part2.3.3V
  N1: Part1.0, Part2.SCL
  N2: Part1.1, Part2.SDA

custom parts:
  Tessel 2: Draft version of Tessel 2
  HTU21D Breakout: This is a breadboard friendly breakout board for the Measurement Specialties high-precision, low-power digital humidity sensor.
