# Fritzing sketch temperature-MCP9808-tessel (saved by Fritzing 0.9.1b)

parts:
  Part5 = MCP9808
  Part6 = Tessel 2

nets:
  N1: Part5.SDA, Part6.1
  N2: Part5.SCL, Part6.0
  VCC: Part5.VCC, Part6.3V3
  GND: Part5.GND, Part6.GND

custom parts:
  Tessel 2: Draft version of Tessel 2
