# Fritzing sketch temperature-MCP9808 (saved by Fritzing 0.9.1b)

parts:
  Part3 = Arduino Uno (Rev3)
  Part5 = MCP9808

nets:
  N1: Part3.A4/SDA, Part5.SDA
  N2: Part3.A5/SCL, Part5.SCL
  5V: Part3.5V, Part5.VCC
  GND: Part3.GND, Part5.GND
