# Fritzing sketch temperature-ds18b20 (saved by Fritzing 0.9.1b)
breadboards: 1

parts:
  Part1 = Arduino Uno (Rev3)
  DS1 = DS18B20 1-Wire Temperature Sensor [part_number=DS18B20]
  R2 = Resistor [tolerance=±5% resistance=4.7k package="0603 [SMD]"]

nets:
  N1: Part1.D2, DS1.DQ, R2.Pin_0
  5V: Part1.5V, DS1.VDD, R2.Pin_1
  GND: Part1.GND, DS1.GND
