# Fritzing sketch temperature-lm335 (saved by Fritzing 0.9.2b)
breadboards: 1

parts:
  T1 = LM35 Temperature Sensor [package="TO92 [THT]"]
  Part1 = Arduino Uno (Rev3)
  R1 = Resistor [tolerance=±5% resistance=2k package=THT]

nets:
  N1: T1.Vout, Part1.A0, R1.Pin_1
  GND: T1.GND, Part1.GND
  N2: Part1.5V, R1.Pin_0
