# Fritzing sketch temperature-max31850k (saved by Fritzing 0.9.2b)
breadboards: 1

parts:
  BREAKOUT1 = MAX31850 Thermocouple Breakout
  Part1 = Logic Level Converter
  Part2 = Arduino Uno (Rev3)
  R1 = Resistor [tolerance=±20% resistance=4.7k package="0402 [SMD]"]

nets:
  GND: BREAKOUT1.GND, Part1.GND, Part2.GND
  VIN: BREAKOUT1.VIN, Part2.3V3, R1.Pin_1
  N1: BREAKOUT1.DATA, R1.Pin_0
  N2: Part1.TX_HV, Part2.D2
  N3: Part1.HV, Part2.5V
