# Fritzing sketch temperature-tmp102 (saved by Fritzing 0.9.1b)

parts:
  Part1 = Digital Temperature Sensor Breakout - TMP102
  Part2 = Arduino Uno (Rev3)

nets:
  N1: Part1.V+, Part2.5V
  N2: Part1.SDA, Part2.A4/SDA
  N3: Part1.SCL, Part2.A5/SCL
  GND: Part1.GND, Part2.GND
