# Fritzing sketch toggle-switch (saved by Fritzing 0.7.10b)
breadboards: 1

parts:
  Arduino1 = Arduino
  S1 = Toggle Switch [package=THT]
  R1 = Resistor [tolerance=±5% resistance=10k package=THT]

nets:
  N1: Arduino1.D8, S1.L1, R1.Pin_1
  N2: Arduino1.+5V, S1.COM
  N3: Arduino1.GND, R1.Pin_0
